// Logisim project 4bitsequencerecognizer.circ as structural Verilog
module _0000Dff (
  input  X,
  input  Reset,
  output Z
);

  wire and_1_out, and_2_out, and_3_out, and_4_out, clock_1_out, not_1_out, or_1_out, or_2_out, Q0_q, Q0_qn,
       Q1_q, Q1_qn;

  Clock clock_1 (.out(clock_1_out));
  not not_1 (not_1_out, X);
  and and_1 (and_1_out, Q0_q, not_1_out);
  and and_2 (and_2_out, Q1_q, not_1_out);
  and and_3 (and_3_out, Q0_qn, not_1_out);
  and and_4 (and_4_out, Q1_q, not_1_out);
  and and_5 (Z, Q1_q, Q0_q, not_1_out);
  or or_1 (or_1_out, and_1_out, and_2_out);
  or or_2 (or_2_out, and_3_out, and_4_out);
  D_Flip_Flop #(.trigger("falling")) Q1 (
    .clk(clock_1_out), .D(or_1_out), .Q(Q1_q), .Qn(Q1_qn), .en(1'b1), .reset(Reset));  // open: preset
  D_Flip_Flop #(.trigger("falling")) Q0 (
    .clk(clock_1_out), .D(or_2_out), .Q(Q0_q), .Qn(Q0_qn), .en(1'b1), .reset(Reset));  // open: preset
endmodule

module _0000JKff (
  input  X,
  input  Reset,
  output Z
);

  wire and_1_out, clock_1_out, not_1_out, or_1_out, Q0_q, Q0_qn, Q1_q, Q1_qn;

  Clock clock_1 (.out(clock_1_out));
  not not_1 (not_1_out, X);
  and and_1 (and_1_out, Q0_q, not_1_out);
  or or_1 (or_1_out, Q1_qn, X);
  and and_2 (Z, Q1_q, Q0_q, not_1_out);
  J_K_Flip_Flop #(.trigger("falling")) Q1 (
    .J(and_1_out), .clk(clock_1_out), .K(X), .Q(Q1_q), .Qn(Q1_qn), .en(1'b1), .reset(Reset));  // open: preset
  J_K_Flip_Flop #(.trigger("falling")) Q0 (
    .J(not_1_out), .clk(clock_1_out), .K(or_1_out), .Q(Q0_q), .Qn(Q0_qn), .en(1'b1), .reset(Reset));  // open: preset
endmodule

module _0000Tff (
  input  X,
  input  Reset,
  output Z
);

  wire and_1_out, and_2_out, and_3_out, and_4_out, and_5_out, clock_1_out, not_1_out, or_1_out, or_2_out,
       Q0_q, Q0_qn, Q1_q, Q1_qn;

  Clock clock_1 (.out(clock_1_out));
  not not_1 (not_1_out, X);
  and and_1 (and_1_out, Q1_q, X);
  and and_2 (and_2_out, Q1_qn, Q0_q, not_1_out);
  and and_3 (and_3_out, Q0_qn, not_1_out);
  and and_4 (and_4_out, Q0_q, X);
  and and_5 (and_5_out, Q1_qn, Q0_q);
  and and_6 (Z, Q1_q, Q0_q, not_1_out);
  or or_1 (or_1_out, and_1_out, and_2_out);
  or or_2 (or_2_out, and_3_out, and_4_out, and_5_out);
  T_Flip_Flop #(.trigger("falling")) Q1 (
    .clk(clock_1_out), .T(or_1_out), .Q(Q1_q), .Qn(Q1_qn), .reset(Reset), .en(1'b1));  // open: preset
  T_Flip_Flop #(.trigger("falling")) Q0 (
    .clk(clock_1_out), .T(or_2_out), .Q(Q0_q), .Qn(Q0_qn), .reset(Reset), .en(1'b1));  // open: preset
endmodule

module _0001Dff (
  input  X,
  input  Reset,
  output Z
);

  wire and_1_out, and_2_out, and_3_out, and_4_out, clock_1_out, not_1_out, or_1_out, or_2_out, Q0_q, Q0_qn,
       Q1_q, Q1_qn;

  Clock clock_1 (.out(clock_1_out));
  not not_1 (not_1_out, X);
  and and_1 (and_1_out, Q0_q, not_1_out);
  and and_2 (and_2_out, Q1_q, not_1_out);
  and and_3 (and_3_out, Q0_qn, not_1_out);
  and and_4 (and_4_out, Q1_q, not_1_out);
  and and_5 (Z, Q1_q, Q0_q, X);
  or or_1 (or_1_out, and_1_out, and_2_out);
  or or_2 (or_2_out, and_3_out, and_4_out);
  D_Flip_Flop #(.trigger("falling")) Q1 (
    .clk(clock_1_out), .D(or_1_out), .Q(Q1_q), .Qn(Q1_qn), .en(1'b1), .reset(Reset));  // open: preset
  D_Flip_Flop #(.trigger("falling")) Q0 (
    .clk(clock_1_out), .D(or_2_out), .Q(Q0_q), .Qn(Q0_qn), .en(1'b1), .reset(Reset));  // open: preset
endmodule

module _0001JKff (
  input  X,
  input  Reset,
  output Z
);

  wire and_1_out, clock_1_out, not_1_out, or_1_out, Q0_q, Q0_qn, Q1_q, Q1_qn;

  Clock clock_1 (.out(clock_1_out));
  not not_1 (not_1_out, X);
  and and_1 (and_1_out, Q0_q, not_1_out);
  or or_1 (or_1_out, Q1_qn, X);
  and and_2 (Z, Q1_q, Q0_q, X);
  J_K_Flip_Flop #(.trigger("falling")) Q1 (
    .J(and_1_out), .clk(clock_1_out), .K(X), .Q(Q1_q), .Qn(Q1_qn), .en(1'b1), .reset(Reset));  // open: preset
  J_K_Flip_Flop #(.trigger("falling")) Q0 (
    .J(not_1_out), .clk(clock_1_out), .K(or_1_out), .Q(Q0_q), .Qn(Q0_qn), .en(1'b1), .reset(Reset));  // open: preset
endmodule

module _0001Tff (
  input  X,
  input  Reset,
  output Z
);

  wire and_1_out, and_2_out, and_3_out, and_4_out, and_5_out, clock_1_out, not_1_out, or_1_out, or_2_out,
       Q0_q, Q0_qn, Q1_q, Q1_qn;

  Clock clock_1 (.out(clock_1_out));
  not not_1 (not_1_out, X);
  and and_1 (and_1_out, Q1_q, X);
  and and_2 (and_2_out, Q1_qn, Q0_q, not_1_out);
  and and_3 (and_3_out, Q0_qn, not_1_out);
  and and_4 (and_4_out, Q0_q, X);
  and and_5 (and_5_out, Q1_qn, Q0_q);
  and and_6 (Z, Q1_q, Q0_q, X);
  or or_1 (or_1_out, and_1_out, and_2_out);
  or or_2 (or_2_out, and_3_out, and_4_out, and_5_out);
  T_Flip_Flop #(.trigger("falling")) Q1 (
    .clk(clock_1_out), .T(or_1_out), .Q(Q1_q), .Qn(Q1_qn), .reset(Reset), .en(1'b1));  // open: preset
  T_Flip_Flop #(.trigger("falling")) Q0 (
    .clk(clock_1_out), .T(or_2_out), .Q(Q0_q), .Qn(Q0_qn), .reset(Reset), .en(1'b1));  // open: preset
endmodule

module _0010Dff (
  input  X,
  input  Reset,
  output Z
);

  wire and_1_out, and_2_out, and_3_out, and_4_out, and_5_out, clock_1_out, not_1_out, or_1_out, or_2_out,
       Q0_q, Q0_qn, Q1_q, Q1_qn;

  Clock clock_1 (.out(clock_1_out));
  not not_1 (not_1_out, X);
  and and_1 (and_1_out, Q1_q, Q0_qn);
  and and_2 (and_2_out, Q1_qn, Q0_q, not_1_out);
  and and_3 (and_3_out, Q1_qn, Q0_qn, not_1_out);
  and and_4 (and_4_out, Q1_q, Q0_qn, X);
  and and_5 (and_5_out, Q1_q, Q0_q, not_1_out);
  and and_6 (Z, Q1_q, Q0_q, not_1_out);
  or or_1 (or_1_out, and_1_out, and_2_out);
  or or_2 (or_2_out, and_3_out, and_4_out, and_5_out);
  D_Flip_Flop #(.trigger("falling")) Q1 (
    .clk(clock_1_out), .D(or_1_out), .Q(Q1_q), .Qn(Q1_qn), .en(1'b1), .reset(Reset));  // open: preset
  D_Flip_Flop #(.trigger("falling")) Q0 (
    .clk(clock_1_out), .D(or_2_out), .Q(Q0_q), .Qn(Q0_qn), .en(1'b1), .reset(Reset));  // open: preset
endmodule

module _0010JKff (
  input  X,
  input  Reset,
  output Z
);

  wire and_1_out, and_2_out, and_3_out, clock_1_out, not_1_out, or_1_out, or_2_out, Q0_q, Q0_qn, Q1_q, Q1_qn;

  Clock clock_1 (.out(clock_1_out));
  not not_1 (not_1_out, X);
  and and_1 (and_1_out, Q0_q, not_1_out);
  and and_2 (and_2_out, Q1_qn, not_1_out);
  and and_3 (and_3_out, Q1_q, X);
  or or_1 (or_1_out, Q1_qn, X);
  and and_4 (Z, Q1_q, Q0_q, not_1_out);
  or or_2 (or_2_out, and_2_out, and_3_out);
  J_K_Flip_Flop #(.trigger("falling")) Q1 (
    .J(and_1_out), .clk(clock_1_out), .K(Q0_q), .Q(Q1_q), .Qn(Q1_qn), .en(1'b1), .reset(Reset));  // open: preset
  J_K_Flip_Flop #(.trigger("falling")) Q0 (
    .J(or_2_out), .clk(clock_1_out), .K(or_1_out), .Q(Q0_q), .Qn(Q0_qn), .en(1'b1), .reset(Reset));  // open: preset
endmodule

module _0010Tff (
  input  X,
  input  Reset,
  output Z
);

  wire and_1_out, and_2_out, and_3_out, and_4_out, and_5_out, clock_1_out, not_1_out, or_1_out, or_2_out,
       Q0_q, Q0_qn, Q1_q, Q1_qn;

  Clock clock_1 (.out(clock_1_out));
  not not_1 (not_1_out, X);
  and and_1 (and_1_out, Q1_q, Q0_q);
  and and_2 (and_2_out, Q0_q, not_1_out);
  and and_3 (and_3_out, Q1_qn, not_1_out);
  and and_4 (and_4_out, Q1_q, X);
  and and_5 (and_5_out, Q0_q, X);
  and and_6 (Z, Q1_q, Q0_q, not_1_out);
  or or_1 (or_1_out, and_1_out, and_2_out);
  or or_2 (or_2_out, and_3_out, and_4_out, and_5_out);
  T_Flip_Flop #(.trigger("falling")) Q1 (
    .clk(clock_1_out), .T(or_1_out), .Q(Q1_q), .Qn(Q1_qn), .reset(Reset), .en(1'b1));  // open: preset
  T_Flip_Flop #(.trigger("falling")) Q0 (
    .clk(clock_1_out), .T(or_2_out), .Q(Q0_q), .Qn(Q0_qn), .reset(Reset), .en(1'b1));  // open: preset
endmodule

module _0011Dff (
  input  X,
  input  Reset,
  output Z
);

  wire and_1_out, and_2_out, and_3_out, and_4_out, and_5_out, clock_1_out, not_1_out, or_1_out, or_2_out,
       Q0_q, Q0_qn, Q1_q, Q1_qn;

  Clock clock_1 (.out(clock_1_out));
  not not_1 (not_1_out, X);
  and and_1 (and_1_out, Q1_q, Q0_qn);
  and and_2 (and_2_out, Q1_qn, Q0_q, not_1_out);
  and and_3 (and_3_out, Q1_qn, Q0_qn, not_1_out);
  and and_4 (and_4_out, Q1_q, Q0_qn, X);
  and and_5 (and_5_out, Q1_q, Q0_q, not_1_out);
  and and_6 (Z, Q1_q, Q0_q, X);
  or or_1 (or_1_out, and_1_out, and_2_out);
  or or_2 (or_2_out, and_3_out, and_4_out, and_5_out);
  D_Flip_Flop #(.trigger("falling")) Q1 (
    .clk(clock_1_out), .D(or_1_out), .Q(Q1_q), .Qn(Q1_qn), .en(1'b1), .reset(Reset));  // open: preset
  D_Flip_Flop #(.trigger("falling")) Q0 (
    .clk(clock_1_out), .D(or_2_out), .Q(Q0_q), .Qn(Q0_qn), .en(1'b1), .reset(Reset));  // open: preset
endmodule

module _0011JKff (
  input  X,
  input  Reset,
  output Z
);

  wire and_1_out, and_2_out, and_3_out, clock_1_out, not_1_out, or_1_out, or_2_out, Q0_q, Q0_qn, Q1_q, Q1_qn;

  Clock clock_1 (.out(clock_1_out));
  not not_1 (not_1_out, X);
  and and_1 (and_1_out, Q0_q, not_1_out);
  and and_2 (and_2_out, Q1_qn, not_1_out);
  and and_3 (and_3_out, Q1_q, X);
  or or_1 (or_1_out, Q1_qn, X);
  and and_4 (Z, Q1_q, Q0_q, X);
  or or_2 (or_2_out, and_2_out, and_3_out);
  J_K_Flip_Flop #(.trigger("falling")) Q1 (
    .J(and_1_out), .clk(clock_1_out), .K(Q0_q), .Q(Q1_q), .Qn(Q1_qn), .en(1'b1), .reset(Reset));  // open: preset
  J_K_Flip_Flop #(.trigger("falling")) Q0 (
    .J(or_2_out), .clk(clock_1_out), .K(or_1_out), .Q(Q0_q), .Qn(Q0_qn), .en(1'b1), .reset(Reset));  // open: preset
endmodule

module _0011Tff (
  input  X,
  input  Reset,
  output Z
);

  wire and_1_out, and_2_out, and_3_out, and_4_out, and_5_out, clock_1_out, not_1_out, or_1_out, or_2_out,
       Q0_q, Q0_qn, Q1_q, Q1_qn;

  Clock clock_1 (.out(clock_1_out));
  not not_1 (not_1_out, X);
  and and_1 (and_1_out, Q1_q, Q0_q);
  and and_2 (and_2_out, Q0_q, not_1_out);
  and and_3 (and_3_out, Q1_qn, not_1_out);
  and and_4 (and_4_out, Q1_q, X);
  and and_5 (and_5_out, Q0_q, X);
  and and_6 (Z, Q1_q, Q0_q, X);
  or or_1 (or_1_out, and_1_out, and_2_out);
  or or_2 (or_2_out, and_3_out, and_4_out, and_5_out);
  T_Flip_Flop #(.trigger("falling")) Q1 (
    .clk(clock_1_out), .T(or_1_out), .Q(Q1_q), .Qn(Q1_qn), .reset(Reset), .en(1'b1));  // open: preset
  T_Flip_Flop #(.trigger("falling")) Q0 (
    .clk(clock_1_out), .T(or_2_out), .Q(Q0_q), .Qn(Q0_qn), .reset(Reset), .en(1'b1));  // open: preset
endmodule

module _0100Dff (
  input  X,
  input  Reset,
  output Z
);

  wire and_1_out, and_2_out, clock_1_out, not_1_out, or_1_out, Q0_q, Q0_qn, Q1_q, Q1_qn;

  Clock clock_1 (.out(clock_1_out));
  not not_1 (not_1_out, X);
  and and_1 (and_1_out, Q0_q, X);
  and and_2 (and_2_out, Q1_q, Q0_qn, not_1_out);
  and and_3 (Z, Q1_q, Q0_q, not_1_out);
  or or_1 (or_1_out, and_1_out, and_2_out);
  D_Flip_Flop #(.trigger("falling")) Q1 (
    .clk(clock_1_out), .D(or_1_out), .Q(Q1_q), .Qn(Q1_qn), .en(1'b1), .reset(Reset));  // open: preset
  D_Flip_Flop #(.trigger("falling")) Q0 (
    .clk(clock_1_out), .D(not_1_out), .Q(Q0_q), .Qn(Q0_qn), .en(1'b1), .reset(Reset));  // open: preset
endmodule

module _0100JKff (
  input  X,
  input  Reset,
  output Z
);

  wire and_1_out, and_2_out, and_3_out, clock_1_out, not_1_out, or_1_out, Q0_q, Q0_qn, Q1_q, Q1_qn;

  Clock clock_1 (.out(clock_1_out));
  not not_1 (not_1_out, X);
  and and_1 (and_1_out, Q0_q, X);
  and and_2 (and_2_out, Q0_qn, X);
  and and_3 (and_3_out, Q0_q, not_1_out);
  and and_4 (Z, Q1_q, Q0_q, not_1_out);
  or or_1 (or_1_out, and_2_out, and_3_out);
  J_K_Flip_Flop #(.trigger("falling")) Q1 (
    .J(and_1_out), .clk(clock_1_out), .K(or_1_out), .Q(Q1_q), .Qn(Q1_qn), .en(1'b1), .reset(Reset));  // open: preset
  J_K_Flip_Flop #(.trigger("falling")) Q0 (
    .J(not_1_out), .clk(clock_1_out), .K(X), .Q(Q0_q), .Qn(Q0_qn), .en(1'b1), .reset(Reset));  // open: preset
endmodule

module _0100Tff (
  input  X,
  input  Reset,
  output Z
);

  wire and_1_out, and_2_out, and_3_out, and_4_out, and_5_out, clock_1_out, not_1_out, or_1_out, or_2_out,
       Q0_q, Q0_qn, Q1_q, Q1_qn;

  Clock clock_1 (.out(clock_1_out));
  not not_1 (not_1_out, X);
  and and_1 (and_1_out, Q1_qn, Q0_q, X);
  and and_2 (and_2_out, Q1_q, Q0_qn, X);
  and and_3 (and_3_out, Q1_q, Q0_q, not_1_out);
  and and_4 (and_4_out, Q0_qn, not_1_out);
  and and_5 (and_5_out, Q0_q, X);
  and and_6 (Z, Q1_q, Q0_q, not_1_out);
  or or_1 (or_1_out, and_1_out, and_2_out, and_3_out);
  or or_2 (or_2_out, and_4_out, and_5_out);
  T_Flip_Flop #(.trigger("falling")) Q1 (
    .clk(clock_1_out), .T(or_1_out), .Q(Q1_q), .Qn(Q1_qn), .reset(Reset), .en(1'b1));  // open: preset
  T_Flip_Flop #(.trigger("falling")) Q0 (
    .clk(clock_1_out), .T(or_2_out), .Q(Q0_q), .Qn(Q0_qn), .reset(Reset), .en(1'b1));  // open: preset
endmodule

module _0101Dff (
  input  X,
  input  Reset,
  output Z
);

  wire and_1_out, and_2_out, clock_1_out, not_1_out, or_1_out, Q0_q, Q0_qn, Q1_q, Q1_qn;

  Clock clock_1 (.out(clock_1_out));
  not not_1 (not_1_out, X);
  and and_1 (and_1_out, Q0_q, X);
  and and_2 (and_2_out, Q1_q, Q0_qn, not_1_out);
  and and_3 (Z, Q1_q, Q0_q, X);
  or or_1 (or_1_out, and_1_out, and_2_out);
  D_Flip_Flop #(.trigger("falling")) Q1 (
    .clk(clock_1_out), .D(or_1_out), .Q(Q1_q), .Qn(Q1_qn), .en(1'b1), .reset(Reset));  // open: preset
  D_Flip_Flop #(.trigger("falling")) Q0 (
    .clk(clock_1_out), .D(not_1_out), .Q(Q0_q), .Qn(Q0_qn), .en(1'b1), .reset(Reset));  // open: preset
endmodule

module _0101JKff (
  input  X,
  input  Reset,
  output Z
);

  wire and_1_out, and_2_out, and_3_out, clock_1_out, not_1_out, or_1_out, Q0_q, Q0_qn, Q1_q, Q1_qn;

  Clock clock_1 (.out(clock_1_out));
  not not_1 (not_1_out, X);
  and and_1 (and_1_out, Q0_q, X);
  and and_2 (and_2_out, Q0_qn, X);
  and and_3 (and_3_out, Q0_q, not_1_out);
  and and_4 (Z, Q1_q, Q0_q, X);
  or or_1 (or_1_out, and_2_out, and_3_out);
  J_K_Flip_Flop #(.trigger("falling")) Q1 (
    .J(and_1_out), .clk(clock_1_out), .K(or_1_out), .Q(Q1_q), .Qn(Q1_qn), .en(1'b1), .reset(Reset));  // open: preset
  J_K_Flip_Flop #(.trigger("falling")) Q0 (
    .J(not_1_out), .clk(clock_1_out), .K(X), .Q(Q0_q), .Qn(Q0_qn), .en(1'b1), .reset(Reset));  // open: preset
endmodule

module _0101Tff (
  input  X,
  input  Reset,
  output Z
);

  wire and_1_out, and_2_out, and_3_out, and_4_out, and_5_out, clock_1_out, not_1_out, or_1_out, or_2_out,
       Q0_q, Q0_qn, Q1_q, Q1_qn;

  Clock clock_1 (.out(clock_1_out));
  not not_1 (not_1_out, X);
  and and_1 (and_1_out, Q1_qn, Q0_q, X);
  and and_2 (and_2_out, Q1_q, Q0_qn, X);
  and and_3 (and_3_out, Q1_q, Q0_q, not_1_out);
  and and_4 (and_4_out, Q0_qn, not_1_out);
  and and_5 (and_5_out, Q0_q, X);
  and and_6 (Z, Q1_q, Q0_q, X);
  or or_1 (or_1_out, and_1_out, and_2_out, and_3_out);
  or or_2 (or_2_out, and_4_out, and_5_out);
  T_Flip_Flop #(.trigger("falling")) Q1 (
    .clk(clock_1_out), .T(or_1_out), .Q(Q1_q), .Qn(Q1_qn), .reset(Reset), .en(1'b1));  // open: preset
  T_Flip_Flop #(.trigger("falling")) Q0 (
    .clk(clock_1_out), .T(or_2_out), .Q(Q0_q), .Qn(Q0_qn), .reset(Reset), .en(1'b1));  // open: preset
endmodule

module _0110Dff (
  input  X,
  input  Reset,
  output Z
);

  wire and_1_out, and_2_out, and_3_out, clock_1_out, not_1_out, or_1_out, or_2_out, Q0_q, Q0_qn, Q1_q, Q1_qn;

  Clock clock_1 (.out(clock_1_out));
  not not_1 (not_1_out, X);
  and and_1 (and_1_out, Q1_q, Q0_qn, X);
  and and_2 (and_2_out, Q1_qn, Q0_q, X);
  and and_3 (and_3_out, Q1_q, Q0_qn);
  and and_4 (Z, Q1_q, Q0_q, not_1_out);
  or or_1 (or_1_out, and_1_out, and_2_out);
  or or_2 (or_2_out, and_3_out, not_1_out);
  D_Flip_Flop #(.trigger("falling")) Q1 (
    .clk(clock_1_out), .D(or_1_out), .Q(Q1_q), .Qn(Q1_qn), .en(1'b1), .reset(Reset));  // open: preset
  D_Flip_Flop #(.trigger("falling")) Q0 (
    .clk(clock_1_out), .D(or_2_out), .Q(Q0_q), .Qn(Q0_qn), .en(1'b1), .reset(Reset));  // open: preset
endmodule

module _0110JKff (
  input  X,
  input  Reset,
  output Z
);

  wire and_1_out, clock_1_out, not_1_out, or_1_out, or_2_out, Q0_q, Q0_qn, Q1_q, Q1_qn;

  Clock clock_1 (.out(clock_1_out));
  not not_1 (not_1_out, X);
  and and_1 (and_1_out, Q0_q, X);
  or or_1 (or_1_out, Q0_q, not_1_out);
  or or_2 (or_2_out, not_1_out, Q1_q);
  and and_2 (Z, Q1_q, Q0_q, not_1_out);
  J_K_Flip_Flop #(.trigger("falling")) Q1 (
    .J(and_1_out), .clk(clock_1_out), .K(or_1_out), .Q(Q1_q), .Qn(Q1_qn), .en(1'b1), .reset(Reset));  // open: preset
  J_K_Flip_Flop #(.trigger("falling")) Q0 (
    .J(or_2_out), .clk(clock_1_out), .K(X), .Q(Q0_q), .Qn(Q0_qn), .en(1'b1), .reset(Reset));  // open: preset
endmodule

module _0110Tff (
  input  X,
  input  Reset,
  output Z
);

  wire and_1_out, and_2_out, and_3_out, and_4_out, and_5_out, and_6_out, and_7_out, clock_1_out, not_1_out,
       or_1_out, or_2_out, Q0_q, Q0_qn, Q1_q, Q1_qn;

  Clock clock_1 (.out(clock_1_out));
  not not_1 (not_1_out, X);
  and and_1 (and_1_out, Q1_q, Q0_q);
  and and_2 (and_2_out, Q0_q, X);
  and and_3 (and_3_out, Q1_q, not_1_out);
  and and_4 (and_4_out, Q0_qn, not_1_out);
  and and_5 (and_5_out, Q1_q, Q0_qn);
  and and_6 (and_6_out, Q1_q, X);
  and and_7 (and_7_out, Q0_q, X);
  and and_8 (Z, Q1_q, Q0_q, not_1_out);
  or or_1 (or_1_out, and_1_out, and_2_out, and_3_out);
  or or_2 (or_2_out, and_4_out, and_5_out, and_6_out, and_7_out);
  T_Flip_Flop #(.trigger("falling")) Q1 (
    .clk(clock_1_out), .T(or_1_out), .Q(Q1_q), .Qn(Q1_qn), .reset(Reset), .en(1'b1));  // open: preset
  T_Flip_Flop #(.trigger("falling")) Q0 (
    .clk(clock_1_out), .T(or_2_out), .Q(Q0_q), .Qn(Q0_qn), .reset(Reset), .en(1'b1));  // open: preset
endmodule

module _0111Dff (
  input  X,
  input  Reset,
  output Z
);

  wire and_1_out, and_2_out, and_3_out, clock_1_out, not_1_out, or_1_out, or_2_out, Q0_q, Q0_qn, Q1_q, Q1_qn;

  Clock clock_1 (.out(clock_1_out));
  not not_1 (not_1_out, X);
  and and_1 (and_1_out, Q1_q, Q0_qn, X);
  and and_2 (and_2_out, Q1_qn, Q0_q, X);
  and and_3 (and_3_out, Q1_q, Q0_qn);
  and and_4 (Z, Q1_q, Q0_q, X);
  or or_1 (or_1_out, and_1_out, and_2_out);
  or or_2 (or_2_out, and_3_out, not_1_out);
  D_Flip_Flop #(.trigger("falling")) Q1 (
    .clk(clock_1_out), .D(or_1_out), .Q(Q1_q), .Qn(Q1_qn), .en(1'b1), .reset(Reset));  // open: preset
  D_Flip_Flop #(.trigger("falling")) Q0 (
    .clk(clock_1_out), .D(or_2_out), .Q(Q0_q), .Qn(Q0_qn), .en(1'b1), .reset(Reset));  // open: preset
endmodule

module _0111JKff (
  input  X,
  input  Reset,
  output Z
);

  wire and_1_out, clock_1_out, not_1_out, or_1_out, or_2_out, Q0_q, Q0_qn, Q1_q, Q1_qn;

  Clock clock_1 (.out(clock_1_out));
  not not_1 (not_1_out, X);
  and and_1 (and_1_out, Q0_q, X);
  or or_1 (or_1_out, Q0_q, not_1_out);
  or or_2 (or_2_out, not_1_out, Q1_q);
  and and_2 (Z, Q1_q, Q0_q, X);
  J_K_Flip_Flop #(.trigger("falling")) Q1 (
    .J(and_1_out), .clk(clock_1_out), .K(or_1_out), .Q(Q1_q), .Qn(Q1_qn), .en(1'b1), .reset(Reset));  // open: preset
  J_K_Flip_Flop #(.trigger("falling")) Q0 (
    .J(or_2_out), .clk(clock_1_out), .K(X), .Q(Q0_q), .Qn(Q0_qn), .en(1'b1), .reset(Reset));  // open: preset
endmodule

module _0111Tff (
  input  X,
  input  Reset,
  output Z
);

  wire and_1_out, and_2_out, and_3_out, and_4_out, and_5_out, and_6_out, and_7_out, clock_1_out, not_1_out,
       or_1_out, or_2_out, Q0_q, Q0_qn, Q1_q, Q1_qn;

  Clock clock_1 (.out(clock_1_out));
  not not_1 (not_1_out, X);
  and and_1 (and_1_out, Q1_q, Q0_q);
  and and_2 (and_2_out, Q0_q, X);
  and and_3 (and_3_out, Q1_q, not_1_out);
  and and_4 (and_4_out, Q0_qn, not_1_out);
  and and_5 (and_5_out, Q1_q, Q0_qn);
  and and_6 (and_6_out, Q1_q, X);
  and and_7 (and_7_out, Q0_q, X);
  and and_8 (Z, Q1_q, Q0_q, X);
  or or_1 (or_1_out, and_1_out, and_2_out, and_3_out);
  or or_2 (or_2_out, and_4_out, and_5_out, and_6_out, and_7_out);
  T_Flip_Flop #(.trigger("falling")) Q1 (
    .clk(clock_1_out), .T(or_1_out), .Q(Q1_q), .Qn(Q1_qn), .reset(Reset), .en(1'b1));  // open: preset
  T_Flip_Flop #(.trigger("falling")) Q0 (
    .clk(clock_1_out), .T(or_2_out), .Q(Q0_q), .Qn(Q0_qn), .reset(Reset), .en(1'b1));  // open: preset
endmodule

module _1000Dff (
  input  X,
  input  Reset,
  output Z
);

  wire and_1_out, and_2_out, and_3_out, clock_1_out, not_1_out, or_1_out, or_2_out, Q0_q, Q0_qn, Q1_q, Q1_qn;

  Clock clock_1 (.out(clock_1_out));
  not not_1 (not_1_out, X);
  and and_1 (and_1_out, Q1_qn, Q0_q, not_1_out);
  and and_2 (and_2_out, Q1_q, Q0_qn, not_1_out);
  and and_3 (and_3_out, Q1_q, Q0_qn);
  and and_4 (Z, Q1_q, Q0_q, not_1_out);
  or or_1 (or_1_out, and_1_out, and_2_out);
  or or_2 (or_2_out, and_3_out, X);
  D_Flip_Flop #(.trigger("falling")) Q1 (
    .clk(clock_1_out), .D(or_1_out), .Q(Q1_q), .Qn(Q1_qn), .en(1'b1), .reset(Reset));  // open: preset
  D_Flip_Flop #(.trigger("falling")) Q0 (
    .clk(clock_1_out), .D(or_2_out), .Q(Q0_q), .Qn(Q0_qn), .en(1'b1), .reset(Reset));  // open: preset
endmodule

module _1000JKff (
  input  X,
  input  Reset,
  output Z
);

  wire and_1_out, and_2_out, and_3_out, clock_1_out, not_1_out, or_1_out, or_2_out, Q0_q, Q0_qn, Q1_q, Q1_qn;

  Clock clock_1 (.out(clock_1_out));
  not not_1 (not_1_out, X);
  and and_1 (and_1_out, Q0_q, not_1_out);
  or or_1 (or_1_out, Q0_q, X);
  and and_2 (and_2_out, Q1_q, not_1_out);
  and and_3 (and_3_out, Q1_qn, X);
  and and_4 (Z, Q1_q, Q0_q, not_1_out);
  or or_2 (or_2_out, and_2_out, and_3_out);
  J_K_Flip_Flop #(.trigger("falling")) Q1 (
    .J(and_1_out), .clk(clock_1_out), .K(or_1_out), .Q(Q1_q), .Qn(Q1_qn), .en(1'b1), .reset(Reset));  // open: preset
  J_K_Flip_Flop #(.trigger("falling")) Q0 (
    .J(or_2_out), .clk(clock_1_out), .K(1'b1), .Q(Q0_q), .Qn(Q0_qn), .en(1'b1), .reset(Reset));  // open: preset
endmodule

module _1000Tff (
  input  X,
  input  Reset,
  output Z
);

  wire and_1_out, and_2_out, and_3_out, and_4_out, and_5_out, clock_1_out, not_1_out, or_1_out, or_2_out,
       Q0_q, Q0_qn, Q1_q, Q1_qn;

  Clock clock_1 (.out(clock_1_out));
  not not_1 (not_1_out, X);
  and and_1 (and_1_out, Q0_q, not_1_out);
  and and_2 (and_2_out, Q1_q, X);
  and and_3 (and_3_out, Q1_q, Q0_qn);
  and and_4 (and_4_out, Q0_qn, X);
  and and_5 (and_5_out, Q0_q, not_1_out);
  and and_6 (Z, Q1_q, Q0_q, not_1_out);
  or or_1 (or_1_out, and_1_out, and_2_out);
  or or_2 (or_2_out, and_3_out, and_4_out, and_5_out);
  T_Flip_Flop #(.trigger("falling")) Q1 (
    .clk(clock_1_out), .T(or_1_out), .Q(Q1_q), .Qn(Q1_qn), .reset(Reset), .en(1'b1));  // open: preset
  T_Flip_Flop #(.trigger("falling")) Q0 (
    .clk(clock_1_out), .T(or_2_out), .Q(Q0_q), .Qn(Q0_qn), .reset(Reset), .en(1'b1));  // open: preset
endmodule

module _1001Dff (
  input  X,
  input  Reset,
  output Z
);

  wire and_1_out, and_2_out, and_3_out, clock_1_out, not_1_out, or_1_out, or_2_out, Q0_q, Q0_qn, Q1_q, Q1_qn;

  Clock clock_1 (.out(clock_1_out));
  not not_1 (not_1_out, X);
  and and_1 (and_1_out, Q1_qn, Q0_q, not_1_out);
  and and_2 (and_2_out, Q1_q, Q0_qn, not_1_out);
  and and_3 (and_3_out, Q1_q, Q0_qn);
  and and_4 (Z, Q1_q, Q0_q, X);
  or or_1 (or_1_out, and_1_out, and_2_out);
  or or_2 (or_2_out, and_3_out, X);
  D_Flip_Flop #(.trigger("falling")) Q1 (
    .clk(clock_1_out), .D(or_1_out), .Q(Q1_q), .Qn(Q1_qn), .en(1'b1), .reset(Reset));  // open: preset
  D_Flip_Flop #(.trigger("falling")) Q0 (
    .clk(clock_1_out), .D(or_2_out), .Q(Q0_q), .Qn(Q0_qn), .en(1'b1), .reset(Reset));  // open: preset
endmodule

module _10011JKff (
  input  X,
  input  Reset,
  output Z
);

  wire and_1_out, and_2_out, and_3_out, clock_1_out, not_1_out, or_1_out, or_2_out, Q0_q, Q0_qn, Q1_q, Q1_qn;

  Clock clock_1 (.out(clock_1_out));
  not not_1 (not_1_out, X);
  and and_1 (and_1_out, Q0_q, not_1_out);
  or or_1 (or_1_out, Q0_q, X);
  and and_2 (and_2_out, Q1_q, not_1_out);
  and and_3 (and_3_out, Q1_qn, X);
  and and_4 (Z, Q1_q, Q0_q, X);
  or or_2 (or_2_out, and_2_out, and_3_out);
  J_K_Flip_Flop #(.trigger("falling")) Q1 (
    .J(and_1_out), .clk(clock_1_out), .K(or_1_out), .Q(Q1_q), .Qn(Q1_qn), .en(1'b1), .reset(Reset));  // open: preset
  J_K_Flip_Flop #(.trigger("falling")) Q0 (
    .J(or_2_out), .clk(clock_1_out), .K(1'b1), .Q(Q0_q), .Qn(Q0_qn), .en(1'b1), .reset(Reset));  // open: preset
endmodule

module _1001Tff (
  input  X,
  input  Reset,
  output Z
);

  wire and_1_out, and_2_out, and_3_out, and_4_out, and_5_out, clock_1_out, not_1_out, or_1_out, or_2_out,
       Q0_q, Q0_qn, Q1_q, Q1_qn;

  Clock clock_1 (.out(clock_1_out));
  not not_1 (not_1_out, X);
  and and_1 (and_1_out, Q0_q, not_1_out);
  and and_2 (and_2_out, Q1_q, X);
  and and_3 (and_3_out, Q1_q, Q0_qn);
  and and_4 (and_4_out, Q0_qn, X);
  and and_5 (and_5_out, Q0_q, not_1_out);
  and and_6 (Z, Q1_q, Q0_q, X);
  or or_1 (or_1_out, and_1_out, and_2_out);
  or or_2 (or_2_out, and_3_out, and_4_out, and_5_out);
  T_Flip_Flop #(.trigger("falling")) Q1 (
    .clk(clock_1_out), .T(or_1_out), .Q(Q1_q), .Qn(Q1_qn), .reset(Reset), .en(1'b1));  // open: preset
  T_Flip_Flop #(.trigger("falling")) Q0 (
    .clk(clock_1_out), .T(or_2_out), .Q(Q0_q), .Qn(Q0_qn), .reset(Reset), .en(1'b1));  // open: preset
endmodule

module _1010Dff (
  input  X,
  input  Reset,
  output Z
);

  wire and_1_out, and_2_out, clock_1_out, not_1_out, or_1_out, Q0_q, Q0_qn, Q1_q, Q1_qn;

  Clock clock_1 (.out(clock_1_out));
  not not_1 (not_1_out, X);
  and and_1 (and_1_out, Q0_q, not_1_out);
  and and_2 (and_2_out, Q1_q, Q0_qn, X);
  and and_3 (Z, Q1_q, Q0_q, not_1_out);
  or or_1 (or_1_out, and_1_out, and_2_out);
  D_Flip_Flop #(.trigger("falling")) Q1 (
    .clk(clock_1_out), .D(or_1_out), .Q(Q1_q), .Qn(Q1_qn), .en(1'b1), .reset(Reset));  // open: preset
  D_Flip_Flop #(.trigger("falling")) Q0 (
    .clk(clock_1_out), .D(X), .Q(Q0_q), .Qn(Q0_qn), .en(1'b1), .reset(Reset));  // open: preset
endmodule

module _1010JKff (
  input  X,
  input  Reset,
  output Z
);

  wire and_1_out, and_2_out, and_3_out, clock_1_out, not_1_out, or_1_out, Q0_q, Q0_qn, Q1_q, Q1_qn;

  Clock clock_1 (.out(clock_1_out));
  not not_1 (not_1_out, X);
  and and_1 (and_1_out, Q0_q, not_1_out);
  and and_2 (and_2_out, Q0_qn, not_1_out);
  and and_3 (and_3_out, Q0_q, X);
  and and_4 (Z, Q1_q, Q0_q, not_1_out);
  or or_1 (or_1_out, and_2_out, and_3_out);
  J_K_Flip_Flop #(.trigger("falling")) Q1 (
    .J(and_1_out), .clk(clock_1_out), .K(or_1_out), .Q(Q1_q), .Qn(Q1_qn), .en(1'b1), .reset(Reset));  // open: preset
  J_K_Flip_Flop #(.trigger("falling")) Q0 (
    .J(X), .clk(clock_1_out), .K(not_1_out), .Q(Q0_q), .Qn(Q0_qn), .en(1'b1), .reset(Reset));  // open: preset
endmodule

module _1010Tff (
  input  X,
  input  Reset,
  output Z
);

  wire and_1_out, and_2_out, and_3_out, and_4_out, and_5_out, clock_1_out, not_1_out, or_1_out, or_2_out,
       Q0_q, Q0_qn, Q1_q, Q1_qn;

  Clock clock_1 (.out(clock_1_out));
  not not_1 (not_1_out, X);
  and and_1 (and_1_out, Q1_q, Q0_qn, not_1_out);
  and and_2 (and_2_out, Q1_q, Q0_q, X);
  and and_3 (and_3_out, Q1_qn, Q0_q, not_1_out);
  and and_4 (and_4_out, Q0_qn, X);
  and and_5 (and_5_out, Q0_qn, not_1_out);
  and and_6 (Z, Q1_q, Q0_q, not_1_out);
  or or_1 (or_1_out, and_1_out, and_2_out, and_3_out);
  or or_2 (or_2_out, and_4_out, and_5_out);
  T_Flip_Flop #(.trigger("falling")) Q1 (
    .clk(clock_1_out), .T(or_1_out), .Q(Q1_q), .Qn(Q1_qn), .reset(Reset), .en(1'b1));  // open: preset
  T_Flip_Flop #(.trigger("falling")) Q0 (
    .clk(clock_1_out), .T(or_2_out), .Q(Q0_q), .Qn(Q0_qn), .reset(Reset), .en(1'b1));  // open: preset
endmodule

module _1011Dff (
  input  X,
  input  Reset,
  output Z
);

  wire and_1_out, and_2_out, clock_1_out, not_1_out, or_1_out, Q0_q, Q0_qn, Q1_q, Q1_qn;

  Clock clock_1 (.out(clock_1_out));
  not not_1 (not_1_out, X);
  and and_1 (and_1_out, Q0_q, not_1_out);
  and and_2 (and_2_out, Q1_q, Q0_qn, X);
  and and_3 (Z, Q1_q, Q0_q, X);
  or or_1 (or_1_out, and_1_out, and_2_out);
  D_Flip_Flop #(.trigger("falling")) Q1 (
    .clk(clock_1_out), .D(or_1_out), .Q(Q1_q), .Qn(Q1_qn), .en(1'b1), .reset(Reset));  // open: preset
  D_Flip_Flop #(.trigger("falling")) Q0 (
    .clk(clock_1_out), .D(X), .Q(Q0_q), .Qn(Q0_qn), .en(1'b1), .reset(Reset));  // open: preset
endmodule

module _1011JKff (
  input  X,
  input  Reset,
  output Z
);

  wire and_1_out, and_2_out, and_3_out, clock_1_out, not_1_out, or_1_out, Q0_q, Q0_qn, Q1_q, Q1_qn;

  Clock clock_1 (.out(clock_1_out));
  not not_1 (not_1_out, X);
  and and_1 (and_1_out, Q0_q, not_1_out);
  and and_2 (and_2_out, Q0_qn, not_1_out);
  and and_3 (and_3_out, Q0_q, X);
  and and_4 (Z, Q1_q, Q0_q, X);
  or or_1 (or_1_out, and_2_out, and_3_out);
  J_K_Flip_Flop #(.trigger("falling")) Q1 (
    .J(and_1_out), .clk(clock_1_out), .K(or_1_out), .Q(Q1_q), .Qn(Q1_qn), .en(1'b1), .reset(Reset));  // open: preset
  J_K_Flip_Flop #(.trigger("falling")) Q0 (
    .J(X), .clk(clock_1_out), .K(not_1_out), .Q(Q0_q), .Qn(Q0_qn), .en(1'b1), .reset(Reset));  // open: preset
endmodule

module _1011Tff (
  input  X,
  input  Reset,
  output Z
);

  wire and_1_out, and_2_out, and_3_out, and_4_out, and_5_out, clock_1_out, not_1_out, or_1_out, or_2_out,
       Q0_q, Q0_qn, Q1_q, Q1_qn;

  Clock clock_1 (.out(clock_1_out));
  not not_1 (not_1_out, X);
  and and_1 (and_1_out, Q1_q, Q0_qn, not_1_out);
  and and_2 (and_2_out, Q1_q, Q0_q, X);
  and and_3 (and_3_out, Q1_qn, Q0_q, not_1_out);
  and and_4 (and_4_out, Q0_qn, X);
  and and_5 (and_5_out, Q0_qn, not_1_out);
  and and_6 (Z, Q1_q, Q0_q, X);
  or or_1 (or_1_out, and_1_out, and_2_out, and_3_out);
  or or_2 (or_2_out, and_4_out, and_5_out);
  T_Flip_Flop #(.trigger("falling")) Q1 (
    .clk(clock_1_out), .T(or_1_out), .Q(Q1_q), .Qn(Q1_qn), .reset(Reset), .en(1'b1));  // open: preset
  T_Flip_Flop #(.trigger("falling")) Q0 (
    .clk(clock_1_out), .T(or_2_out), .Q(Q0_q), .Qn(Q0_qn), .reset(Reset), .en(1'b1));  // open: preset
endmodule

module _1100Dff (
  input  X,
  input  Reset,
  output Z
);

  wire and_1_out, and_2_out, and_3_out, and_4_out, and_5_out, clock_1_out, not_1_out, or_1_out, or_2_out,
       Q0_q, Q0_qn, Q1_q, Q1_qn;

  Clock clock_1 (.out(clock_1_out));
  not not_1 (not_1_out, X);
  and and_1 (and_1_out, Q1_q, Q0_qn);
  and and_2 (and_2_out, Q1_qn, Q0_q, X);
  and and_3 (and_3_out, Q1_q, Q0_qn, not_1_out);
  and and_4 (and_4_out, Q1_q, Q0_q, X);
  and and_5 (and_5_out, Q1_qn, Q0_qn, X);
  and and_6 (Z, Q1_q, Q0_q, not_1_out);
  or or_1 (or_1_out, and_1_out, and_2_out);
  or or_2 (or_2_out, and_3_out, and_4_out, and_5_out);
  D_Flip_Flop #(.trigger("falling")) Q1 (
    .clk(clock_1_out), .D(or_1_out), .Q(Q1_q), .Qn(Q1_qn), .en(1'b1), .reset(Reset));  // open: preset
  D_Flip_Flop #(.trigger("falling")) Q0 (
    .clk(clock_1_out), .D(or_2_out), .Q(Q0_q), .Qn(Q0_qn), .en(1'b1), .reset(Reset));  // open: preset
endmodule

module _1100JKff (
  input  X,
  input  Reset,
  output Z
);

  wire and_1_out, and_2_out, and_3_out, clock_1_out, not_1_out, or_1_out, or_2_out, Q0_q, Q0_qn, Q1_q, Q1_qn;

  Clock clock_1 (.out(clock_1_out));
  not not_1 (not_1_out, X);
  and and_1 (and_1_out, Q0_q, X);
  and and_2 (and_2_out, Q1_q, not_1_out);
  and and_3 (and_3_out, Q1_qn, X);
  or or_1 (or_1_out, Q1_qn, not_1_out);
  and and_4 (Z, Q1_q, Q0_q, not_1_out);
  or or_2 (or_2_out, and_2_out, and_3_out);
  J_K_Flip_Flop #(.trigger("falling")) Q1 (
    .J(and_1_out), .clk(clock_1_out), .K(Q0_q), .Q(Q1_q), .Qn(Q1_qn), .en(1'b1), .reset(Reset));  // open: preset
  J_K_Flip_Flop #(.trigger("falling")) Q0 (
    .J(or_2_out), .clk(clock_1_out), .K(or_1_out), .Q(Q0_q), .Qn(Q0_qn), .en(1'b1), .reset(Reset));  // open: preset
endmodule

module _1100Tff (
  input  X,
  input  Reset,
  output Z
);

  wire and_1_out, and_2_out, and_3_out, and_4_out, and_5_out, clock_1_out, not_1_out, or_1_out, or_2_out,
       Q0_q, Q0_qn, Q1_q, Q1_qn;

  Clock clock_1 (.out(clock_1_out));
  not not_1 (not_1_out, X);
  and and_1 (and_1_out, Q0_q, X);
  and and_2 (and_2_out, Q1_q, Q0_q);
  and and_3 (and_3_out, Q1_qn, X);
  and and_4 (and_4_out, Q0_q, not_1_out);
  and and_5 (and_5_out, Q1_q, not_1_out);
  and and_6 (Z, Q1_q, Q0_q, not_1_out);
  or or_1 (or_1_out, and_1_out, and_2_out);
  or or_2 (or_2_out, and_3_out, and_4_out, and_5_out);
  T_Flip_Flop #(.trigger("falling")) Q1 (
    .clk(clock_1_out), .T(or_1_out), .Q(Q1_q), .Qn(Q1_qn), .reset(Reset), .en(1'b1));  // open: preset
  T_Flip_Flop #(.trigger("falling")) Q0 (
    .clk(clock_1_out), .T(or_2_out), .Q(Q0_q), .Qn(Q0_qn), .reset(Reset), .en(1'b1));  // open: preset
endmodule

module _1101Dff (
  input  X,
  input  Reset,
  output Z
);

  wire and_1_out, and_2_out, and_3_out, and_4_out, and_5_out, clock_1_out, not_1_out, or_1_out, or_2_out,
       Q0_q, Q0_qn, Q1_q, Q1_qn;

  Clock clock_1 (.out(clock_1_out));
  not not_1 (not_1_out, X);
  and and_1 (and_1_out, Q1_q, Q0_qn);
  and and_2 (and_2_out, Q1_qn, Q0_q, X);
  and and_3 (and_3_out, Q1_q, Q0_qn, not_1_out);
  and and_4 (and_4_out, Q1_q, Q0_q, X);
  and and_5 (and_5_out, Q1_qn, Q0_qn, X);
  and and_6 (Z, Q1_q, Q0_q, X);
  or or_1 (or_1_out, and_1_out, and_2_out);
  or or_2 (or_2_out, and_3_out, and_4_out, and_5_out);
  D_Flip_Flop #(.trigger("falling")) Q1 (
    .clk(clock_1_out), .D(or_1_out), .Q(Q1_q), .Qn(Q1_qn), .en(1'b1), .reset(Reset));  // open: preset
  D_Flip_Flop #(.trigger("falling")) Q0 (
    .clk(clock_1_out), .D(or_2_out), .Q(Q0_q), .Qn(Q0_qn), .en(1'b1), .reset(Reset));  // open: preset
endmodule

module _1101JKff (
  input  X,
  input  Reset,
  output Z
);

  wire and_1_out, and_2_out, and_3_out, clock_1_out, not_1_out, or_1_out, or_2_out, Q0_q, Q0_qn, Q1_q, Q1_qn;

  Clock clock_1 (.out(clock_1_out));
  not not_1 (not_1_out, X);
  and and_1 (and_1_out, Q0_q, X);
  and and_2 (and_2_out, Q1_q, not_1_out);
  and and_3 (and_3_out, Q1_qn, X);
  or or_1 (or_1_out, Q1_qn, not_1_out);
  and and_4 (Z, Q1_q, Q0_q, X);
  or or_2 (or_2_out, and_2_out, and_3_out);
  J_K_Flip_Flop #(.trigger("falling")) Q1 (
    .J(and_1_out), .clk(clock_1_out), .K(Q0_q), .Q(Q1_q), .Qn(Q1_qn), .en(1'b1), .reset(Reset));  // open: preset
  J_K_Flip_Flop #(.trigger("falling")) Q0 (
    .J(or_2_out), .clk(clock_1_out), .K(or_1_out), .Q(Q0_q), .Qn(Q0_qn), .en(1'b1), .reset(Reset));  // open: preset
endmodule

module _1101Tff (
  input  X,
  input  Reset,
  output Z
);

  wire and_1_out, and_2_out, and_3_out, and_4_out, and_5_out, clock_1_out, not_1_out, or_1_out, or_2_out,
       Q0_q, Q0_qn, Q1_q, Q1_qn;

  Clock clock_1 (.out(clock_1_out));
  not not_1 (not_1_out, X);
  and and_1 (and_1_out, Q0_q, X);
  and and_2 (and_2_out, Q1_q, Q0_q);
  and and_3 (and_3_out, Q1_qn, X);
  and and_4 (and_4_out, Q0_q, not_1_out);
  and and_5 (and_5_out, Q1_q, not_1_out);
  and and_6 (Z, Q1_q, Q0_q, X);
  or or_1 (or_1_out, and_1_out, and_2_out);
  or or_2 (or_2_out, and_3_out, and_4_out, and_5_out);
  T_Flip_Flop #(.trigger("falling")) Q1 (
    .clk(clock_1_out), .T(or_1_out), .Q(Q1_q), .Qn(Q1_qn), .reset(Reset), .en(1'b1));  // open: preset
  T_Flip_Flop #(.trigger("falling")) Q0 (
    .clk(clock_1_out), .T(or_2_out), .Q(Q0_q), .Qn(Q0_qn), .reset(Reset), .en(1'b1));  // open: preset
endmodule

module _1110Dff (
  input  X,
  input  Reset,
  output Z
);

  wire and_1_out, and_2_out, clock_1_out, not_1_out, or_1_out, Q0_q, Q0_qn, Q1_q, Q1_qn;

  Clock clock_1 (.out(clock_1_out));
  not not_1 (not_1_out, X);
  and and_1 (and_1_out, Q1_q, X);
  and and_2 (and_2_out, Q0_q, X);
  and and_3 (Z, Q1_q, Q0_q, not_1_out);
  or or_1 (or_1_out, and_1_out, and_2_out);
  D_Flip_Flop #(.trigger("falling")) Q1 (
    .clk(clock_1_out), .D(or_1_out), .Q(Q1_q), .Qn(Q1_qn), .en(1'b1), .reset(Reset));  // open: preset
  D_Flip_Flop #(.trigger("falling")) Q0 (
    .clk(clock_1_out), .D(X), .Q(Q0_q), .Qn(Q0_qn), .en(1'b1), .reset(Reset));  // open: preset
endmodule

module _1110JKff (
  input  X,
  input  Reset,
  output Z
);

  wire and_1_out, clock_1_out, not_1_out, Q0_q, Q0_qn, Q1_q, Q1_qn;

  Clock clock_1 (.out(clock_1_out));
  not not_1 (not_1_out, X);
  and and_1 (and_1_out, Q0_q, X);
  and and_2 (Z, Q1_q, Q0_q, not_1_out);
  J_K_Flip_Flop #(.trigger("falling")) Q1 (
    .J(and_1_out), .clk(clock_1_out), .K(not_1_out), .Q(Q1_q), .Qn(Q1_qn), .en(1'b1), .reset(Reset));  // open: preset
  J_K_Flip_Flop #(.trigger("falling")) Q0 (
    .J(X), .clk(clock_1_out), .K(not_1_out), .Q(Q0_q), .Qn(Q0_qn), .en(1'b1), .reset(Reset));  // open: preset
endmodule

module _1110Tff (
  input  X,
  input  Reset,
  output Z
);

  wire and_1_out, and_2_out, and_3_out, and_4_out, and_5_out, and_6_out, clock_1_out, not_1_out, or_1_out,
       or_2_out, Q0_q, Q0_qn, Q1_q, Q1_qn;

  Clock clock_1 (.out(clock_1_out));
  not not_1 (not_1_out, X);
  and and_1 (and_1_out, Q1_qn, Q0_q, X);
  and and_2 (and_2_out, Q1_q, Q0_qn, not_1_out);
  and and_3 (and_3_out, Q1_q, Q0_q, not_1_out);
  and and_4 (and_4_out, Q0_qn, X);
  and and_5 (and_5_out, Q1_qn, X);
  and and_6 (and_6_out, Q0_q, not_1_out);
  and and_7 (Z, Q1_q, Q0_q, not_1_out);
  or or_1 (or_1_out, and_1_out, and_2_out, and_3_out);
  or or_2 (or_2_out, and_4_out, and_5_out, and_6_out);
  T_Flip_Flop #(.trigger("falling")) Q1 (
    .clk(clock_1_out), .T(or_1_out), .Q(Q1_q), .Qn(Q1_qn), .reset(Reset), .en(1'b1));  // open: preset
  T_Flip_Flop #(.trigger("falling")) Q0 (
    .clk(clock_1_out), .T(or_2_out), .Q(Q0_q), .Qn(Q0_qn), .reset(Reset), .en(1'b1));  // open: preset
endmodule

module _1111Dff (
  input  X,
  input  Reset,
  output Z
);

  wire and_1_out, and_2_out, clock_1_out, not_1_out, or_1_out, Q0_q, Q0_qn, Q1_q, Q1_qn;

  Clock clock_1 (.out(clock_1_out));
  not not_1 (not_1_out, X);
  and and_1 (and_1_out, Q1_q, X);
  and and_2 (and_2_out, Q0_q, X);
  and and_3 (Z, Q1_q, Q0_q, X);
  or or_1 (or_1_out, and_1_out, and_2_out);
  D_Flip_Flop #(.trigger("falling")) Q1 (
    .clk(clock_1_out), .D(or_1_out), .Q(Q1_q), .Qn(Q1_qn), .en(1'b1), .reset(Reset));  // open: preset
  D_Flip_Flop #(.trigger("falling")) Q0 (
    .clk(clock_1_out), .D(X), .Q(Q0_q), .Qn(Q0_qn), .en(1'b1), .reset(Reset));  // open: preset
endmodule

module _1111JKff (
  input  X,
  input  Reset,
  output Z
);

  wire and_1_out, clock_1_out, not_1_out, Q0_q, Q0_qn, Q1_q, Q1_qn;

  Clock clock_1 (.out(clock_1_out));
  not not_1 (not_1_out, X);
  and and_1 (and_1_out, Q0_q, X);
  and and_2 (Z, Q1_q, Q0_q, X);
  J_K_Flip_Flop #(.trigger("falling")) Q1 (
    .J(and_1_out), .clk(clock_1_out), .K(not_1_out), .Q(Q1_q), .Qn(Q1_qn), .en(1'b1), .reset(Reset));  // open: preset
  J_K_Flip_Flop #(.trigger("falling")) Q0 (
    .J(X), .clk(clock_1_out), .K(not_1_out), .Q(Q0_q), .Qn(Q0_qn), .en(1'b1), .reset(Reset));  // open: preset
endmodule

module _1111Tff (
  input  X,
  input  Reset,
  output Z
);

  wire and_1_out, and_2_out, and_3_out, and_4_out, and_5_out, and_6_out, clock_1_out, not_1_out, or_1_out,
       or_2_out, Q0_q, Q0_qn, Q1_q, Q1_qn;

  Clock clock_1 (.out(clock_1_out));
  not not_1 (not_1_out, X);
  and and_1 (and_1_out, Q1_qn, Q0_q, X);
  and and_2 (and_2_out, Q1_q, Q0_qn, not_1_out);
  and and_3 (and_3_out, Q1_q, Q0_q, not_1_out);
  and and_4 (and_4_out, Q0_qn, X);
  and and_5 (and_5_out, Q1_qn, X);
  and and_6 (and_6_out, Q0_q, not_1_out);
  and and_7 (Z, Q1_q, Q0_q, X);
  or or_1 (or_1_out, and_1_out, and_2_out, and_3_out);
  or or_2 (or_2_out, and_4_out, and_5_out, and_6_out);
  T_Flip_Flop #(.trigger("falling")) Q1 (
    .clk(clock_1_out), .T(or_1_out), .Q(Q1_q), .Qn(Q1_qn), .reset(Reset), .en(1'b1));  // open: preset
  T_Flip_Flop #(.trigger("falling")) Q0 (
    .clk(clock_1_out), .T(or_2_out), .Q(Q0_q), .Qn(Q0_qn), .reset(Reset), .en(1'b1));  // open: preset
endmodule
