// Logisim project AsyncronousCounter.circ as structural Verilog: 3 circuits, main circuit main
module main (
  input  RESET,
  input  RESET_2,
  input  RESET_3,
  input  RESET_4,
  output out_5,
  output out_6,
  output out_7,
  output out_8,
  output out_9,
  output out_10,
  output out_11,
  output out_12,
  output out_13,
  output out_14,
  output out_15,
  output out_16,
  output out_17,
  output out_18,
  output out_19,
  output out_20
);

  wire clock_1_out, clock_2_out, clock_3_out, clock_4_out, j_k_ff_2_qn, j_k_ff_4_q, j_k_ff_6_qn, j_k_ff_8_q,
       j_k_ff_11_qn, j_k_ff_12_q;

  Clock clock_1 (.out(clock_1_out));
  Clock clock_2 (.out(clock_2_out));
  Clock clock_3 (.out(clock_3_out));
  Clock clock_4 (.out(clock_4_out));
  J_K_Flip_Flop #(.trigger("falling")) j_k_ff_1 (
    .J(1'b1), .clk(clock_1_out), .K(1'b1), .Q(out_8), .en(1'b1), .reset(RESET));  // open: Qn, preset
  J_K_Flip_Flop j_k_ff_2 (
    .J(1'b1), .clk(clock_2_out), .K(1'b1), .Q(out_12), .Qn(j_k_ff_2_qn), .en(1'b1), .reset(RESET_2));  // open: preset
  J_K_Flip_Flop #(.trigger("falling")) j_k_ff_3 (
    .J(1'b1), .clk(clock_3_out), .K(1'b1), .Qn(out_16), .en(1'b1), .reset(RESET_3));  // open: Q, preset
  J_K_Flip_Flop j_k_ff_4 (
    .J(1'b1), .clk(clock_4_out), .K(1'b1), .Q(j_k_ff_4_q), .Qn(out_20), .en(1'b1), .reset(RESET_4));  // open: preset
  J_K_Flip_Flop #(.trigger("falling")) j_k_ff_5 (
    .J(1'b1), .clk(out_8), .K(1'b1), .Q(out_7), .en(1'b1), .reset(RESET));  // open: Qn, preset
  J_K_Flip_Flop j_k_ff_6 (
    .J(1'b1), .clk(j_k_ff_2_qn), .K(1'b1), .Q(out_11), .Qn(j_k_ff_6_qn), .en(1'b1), .reset(RESET_2));  // open: preset
  J_K_Flip_Flop #(.trigger("falling")) j_k_ff_7 (
    .J(1'b1), .clk(out_16), .K(1'b1), .Qn(out_15), .en(1'b1), .reset(RESET_3));  // open: Q, preset
  J_K_Flip_Flop j_k_ff_8 (
    .J(1'b1), .clk(j_k_ff_4_q), .K(1'b1), .Q(j_k_ff_8_q), .Qn(out_19), .en(1'b1), .reset(RESET_4));  // open: preset
  J_K_Flip_Flop #(.trigger("falling")) j_k_ff_9 (
    .J(1'b1), .clk(out_7), .K(1'b1), .Q(out_6), .en(1'b1), .reset(RESET));  // open: Qn, preset
  J_K_Flip_Flop #(.trigger("falling")) j_k_ff_10 (
    .J(1'b1), .clk(out_15), .K(1'b1), .Qn(out_14), .en(1'b1), .reset(RESET_3));  // open: Q, preset
  J_K_Flip_Flop j_k_ff_11 (
    .J(1'b1), .clk(j_k_ff_6_qn), .K(1'b1), .Q(out_10), .Qn(j_k_ff_11_qn), .en(1'b1), .reset(RESET_2));  // open: preset
  J_K_Flip_Flop j_k_ff_12 (
    .J(1'b1), .clk(j_k_ff_8_q), .K(1'b1), .Q(j_k_ff_12_q), .Qn(out_18), .en(1'b1), .reset(RESET_4));  // open: preset
  J_K_Flip_Flop #(.trigger("falling")) j_k_ff_13 (
    .J(1'b1), .clk(out_6), .K(1'b1), .Q(out_5), .en(1'b1), .reset(RESET));  // open: Qn, preset
  J_K_Flip_Flop #(.trigger("falling")) j_k_ff_14 (
    .J(1'b1), .clk(out_14), .K(1'b1), .Qn(out_13), .en(1'b1), .reset(RESET_3));  // open: Q, preset
  J_K_Flip_Flop j_k_ff_15 (
    .J(1'b1), .clk(j_k_ff_11_qn), .K(1'b1), .Q(out_9), .en(1'b1), .reset(RESET_2));  // open: Qn, preset
  J_K_Flip_Flop j_k_ff_16 (
    .J(1'b1), .clk(j_k_ff_12_q), .K(1'b1), .Qn(out_17), .en(1'b1), .reset(RESET_4));  // open: Q, preset

  // Notes on the sheet:
  //   Asynchronous up counter falling edge or negative clock
  //   Asynchronous up counter falling edge or negative clock
  //   Asynchronous up counter rising edge positive clock
  //   Asynchronous up counter rising edge positive clock
endmodule

module down (
  input  RESET,
  input  RESET_2,
  input  RESET_3,
  input  RESET_4,
  output out_5,
  output out_6,
  output out_7,
  output out_8,
  output out_9,
  output out_10,
  output out_11,
  output out_12,
  output out_13,
  output out_14,
  output out_15,
  output out_16,
  output out_17,
  output out_18,
  output out_19,
  output out_20
);

  wire clock_1_out, clock_2_out, clock_3_out, clock_4_out, j_k_ff_1_q, j_k_ff_3_qn, j_k_ff_5_q, j_k_ff_7_qn,
       j_k_ff_10_qn, j_k_ff_11_q;

  Clock clock_1 (.out(clock_1_out));
  Clock clock_2 (.out(clock_2_out));
  Clock clock_3 (.out(clock_3_out));
  Clock clock_4 (.out(clock_4_out));
  J_K_Flip_Flop #(.trigger("falling")) j_k_ff_1 (
    .J(1'b1), .clk(clock_1_out), .K(1'b1), .Q(j_k_ff_1_q), .Qn(out_8), .en(1'b1), .reset(RESET));  // open: preset
  J_K_Flip_Flop j_k_ff_2 (
    .J(1'b1), .clk(clock_2_out), .K(1'b1), .Qn(out_12), .en(1'b1), .reset(RESET_2));  // open: Q, preset
  J_K_Flip_Flop #(.trigger("falling")) j_k_ff_3 (
    .J(1'b1), .clk(clock_3_out), .K(1'b1), .Q(out_16), .Qn(j_k_ff_3_qn), .en(1'b1), .reset(RESET_3));  // open: preset
  J_K_Flip_Flop j_k_ff_4 (
    .J(1'b1), .clk(clock_4_out), .K(1'b1), .Q(out_20), .en(1'b1), .reset(RESET_4));  // open: Qn, preset
  J_K_Flip_Flop #(.trigger("falling")) j_k_ff_5 (
    .J(1'b1), .clk(j_k_ff_1_q), .K(1'b1), .Q(j_k_ff_5_q), .Qn(out_7), .en(1'b1), .reset(RESET));  // open: preset
  J_K_Flip_Flop j_k_ff_6 (
    .J(1'b1), .clk(out_12), .K(1'b1), .Qn(out_11), .en(1'b1), .reset(RESET_2));  // open: Q, preset
  J_K_Flip_Flop #(.trigger("falling")) j_k_ff_7 (
    .J(1'b1), .clk(j_k_ff_3_qn), .K(1'b1), .Q(out_15), .Qn(j_k_ff_7_qn), .en(1'b1), .reset(RESET_3));  // open: preset
  J_K_Flip_Flop j_k_ff_8 (
    .J(1'b1), .clk(out_20), .K(1'b1), .Q(out_19), .en(1'b1), .reset(RESET_4));  // open: Qn, preset
  J_K_Flip_Flop j_k_ff_9 (
    .J(1'b1), .clk(out_11), .K(1'b1), .Qn(out_10), .en(1'b1), .reset(RESET_2));  // open: Q, preset
  J_K_Flip_Flop #(.trigger("falling")) j_k_ff_10 (
    .J(1'b1), .clk(j_k_ff_7_qn), .K(1'b1), .Q(out_14), .Qn(j_k_ff_10_qn), .en(1'b1), .reset(RESET_3));  // open: preset
  J_K_Flip_Flop #(.trigger("falling")) j_k_ff_11 (
    .J(1'b1), .clk(j_k_ff_5_q), .K(1'b1), .Q(j_k_ff_11_q), .Qn(out_6), .en(1'b1), .reset(RESET));  // open: preset
  J_K_Flip_Flop j_k_ff_12 (
    .J(1'b1), .clk(out_19), .K(1'b1), .Q(out_18), .en(1'b1), .reset(RESET_4));  // open: Qn, preset
  J_K_Flip_Flop j_k_ff_13 (.J(1'b1), .clk(out_10), .K(1'b1), .Qn(out_9), .en(1'b1));  // open: Q, preset, reset
  J_K_Flip_Flop #(.trigger("falling")) j_k_ff_14 (
    .J(1'b1), .clk(j_k_ff_10_qn), .K(1'b1), .Q(out_13), .en(1'b1), .reset(RESET_3));  // open: Qn, preset
  J_K_Flip_Flop #(.trigger("falling")) j_k_ff_15 (
    .J(1'b1), .clk(j_k_ff_11_q), .K(1'b1), .Qn(out_5), .en(1'b1), .reset(RESET));  // open: Q, preset
  J_K_Flip_Flop j_k_ff_16 (.J(1'b1), .clk(out_18), .K(1'b1), .Q(out_17), .en(1'b1));  // open: Qn, preset, reset

  // Notes on the sheet:
  //   Asynchronous down counter rising edge positive clock
  //   Asynchronous down counter falling edge or negative clock
  //   Asynchronous down counter falling edge or negative clock
  //   Asynchronous down counter rising edge positive clock
endmodule

module practice1 (
  input  in_1,
  output out_2,
  output out_3,
  output out_4
);

  wire clock_1_out;

  Clock clock_1 (.out(clock_1_out));
  J_K_Flip_Flop j_k_ff_1 (
    .J(1'b1), .clk(clock_1_out), .K(1'b1), .Qn(out_4), .en(1'b1), .reset(in_1));  // open: Q, preset
  D_Flip_Flop d_ff_1 (.clk(out_4), .D(out_3), .Qn(out_3), .en(1'b1), .reset(in_1));  // open: Q, preset
  T_Flip_Flop t_ff_1 (.clk(out_3), .T(1'b1), .Qn(out_2), .reset(in_1), .en(1'b1));  // open: Q, preset
endmodule
