// Logisim project PriorityEncoder.circ as structural Verilog: 15 circuits, main circuit main
module main (
  input  D1,
  input  D2,
  input  D0,
  input  D3,
  output A2,
  output A1,
  output A0
);

  wire and_3_out, not_1_out, not_2_out, not_3_out, not_4_out;

  not not_1 (not_1_out, D1);
  not not_2 (not_2_out, D0);
  not not_3 (not_3_out, D2);
  not not_4 (not_4_out, D3);
  and and_1 (A2, not_1_out, not_3_out, not_2_out, D3);
  and and_2 (A1, not_1_out, D2);
  and and_3 (and_3_out, not_1_out, not_3_out, not_2_out, D3);
  or or_1 (A0, and_3_out, D1);

  // Notes on the sheet:
  //   Fall 2021
  //   D1>D2>D0>D3
  //   D0-000
  //   D1-001
  //   D2-010
  //   D3-101
endmodule

module spring22 (
  input  F,
  input  B,
  input  S,
  input  D,
  input  W,
  output A2,
  output A1,
  output A0
);

  wire and_1_out, and_2_out, and_3_out, and_4_out, and_5_out, and_6_out, not_1_out, not_2_out, not_3_out,
       not_4_out, not_5_out;

  not not_1 (not_1_out, F);
  not not_2 (not_2_out, B);
  not not_3 (not_3_out, S);
  not not_4 (not_4_out, D);
  not not_5 (not_5_out, W);
  and and_1 (and_1_out, not_1_out, B);
  and and_2 (and_2_out, not_1_out, not_2_out, S);
  and and_3 (and_3_out, not_1_out, not_2_out, S);
  and and_4 (and_4_out, not_1_out, not_2_out, not_3_out, D);
  and and_5 (and_5_out, not_1_out, not_2_out, S);
  and and_6 (and_6_out, not_1_out, not_2_out, not_3_out, not_4_out, W);
  or or_1 (A2, and_1_out, and_2_out);
  or or_2 (A1, and_3_out, F, and_4_out);
  or or_3 (A0, and_5_out, F, and_6_out);

  // Notes on the sheet:
  //   Spring 2022
  //   F>B>S>D>W
  //   F-011
  //   W-001
  //   B-100
  //   S-111
  //   D-010
endmodule

module Summer2022 (
  input  NO,
  input  NE,
  input  SW,
  input  WE,
  input  EA,
  input  SO,
  output A2,
  output A1,
  output A0
);

  wire and_1_out, and_2_out, and_3_out, and_4_out, and_5_out, not_1_out, not_2_out, not_3_out, not_4_out,
       not_5_out, not_6_out;

  not not_1 (not_1_out, NO);
  not not_2 (not_2_out, NE);
  not not_3 (not_3_out, SW);
  not not_4 (not_4_out, WE);
  not not_5 (not_5_out, EA);
  not not_6 (not_6_out, SO);
  and and_1 (and_1_out, not_1_out, not_2_out, not_3_out, WE);
  and and_2 (and_2_out, not_1_out, not_2_out, not_3_out, not_4_out, not_5_out, SO);
  and and_3 (and_3_out, not_1_out, not_2_out, SW);
  and and_4 (and_4_out, not_1_out, not_2_out, not_3_out, not_4_out, EA);
  and and_5 (and_5_out, not_1_out, NE);
  or or_1 (A2, and_1_out, and_2_out);
  or or_2 (A1, and_2_out, and_3_out, and_4_out);
  or or_3 (A0, and_1_out, and_4_out, and_5_out);

  // Notes on the sheet:
  //   Summer 2022
endmodule

module Fall22 (
  input  F,
  input  K,
  input  D,
  input  E,
  input  U,
  input  T,
  output A2,
  output A1,
  output A0
);

  wire and_1_out, and_2_out, and_3_out, and_4_out, and_5_out, and_6_out, and_7_out, and_8_out, not_1_out,
       not_2_out, not_3_out, not_4_out, not_5_out, not_6_out;

  not not_1 (not_1_out, F);
  not not_2 (not_2_out, K);
  not not_3 (not_3_out, D);
  not not_4 (not_4_out, E);
  not not_5 (not_5_out, U);
  not not_6 (not_6_out, T);
  and and_1 (and_1_out, not_1_out, K);
  and and_2 (and_2_out, not_1_out, not_2_out, not_3_out, not_4_out, U);
  and and_3 (and_3_out, not_1_out, K);
  and and_4 (and_4_out, not_1_out, not_2_out, D);
  and and_5 (and_5_out, not_1_out, not_2_out, not_3_out, E);
  and and_6 (and_6_out, not_1_out, K);
  and and_7 (and_7_out, not_1_out, not_2_out, D);
  and and_8 (and_8_out, not_1_out, not_2_out, not_3_out, not_4_out, not_5_out, T);
  or or_1 (A1, and_3_out, and_4_out, and_5_out);
  or or_2 (A2, F, and_1_out, and_2_out);
  or or_3 (A0, and_6_out, F, and_7_out, and_8_out);

  // Notes on the sheet:
  //   Fall 2022
endmodule

module Spring2023 (
  input  M,
  input  L,
  input  S,
  input  J,
  input  I,
  output A2,
  output A1,
  output A0
);

  wire and_1_out, and_2_out, and_3_out, not_1_out, not_2_out, not_3_out, not_4_out, not_5_out;

  not not_1 (not_1_out, M);
  not not_2 (not_2_out, L);
  not not_3 (not_3_out, S);
  not not_4 (not_4_out, I);
  not not_5 (not_5_out, J);
  and and_1 (and_1_out, not_1_out, L);
  and and_2 (and_2_out, not_1_out, not_2_out, not_3_out, J);
  and and_3 (and_3_out, not_1_out, not_2_out, not_3_out, not_5_out, I);
  or or_1 (A2, M, and_1_out, and_2_out, and_3_out);
  or or_2 (A1, and_1_out, and_3_out);
  or or_3 (A0, M, and_1_out);

  // Notes on the sheet:
  //   Spring 2023
endmodule

module Summer23 (
  input  F,
  input  M,
  input  D,
  input  W,
  output A2,
  output A1,
  output A0
);

  wire and_1_out, and_2_out, and_3_out, not_1_out, not_2_out, not_3_out, not_4_out;

  not not_1 (not_1_out, F);
  not not_2 (not_2_out, D);
  not not_3 (not_3_out, M);
  not not_4 (not_4_out, W);
  and and_1 (and_1_out, not_1_out, not_3_out, D);
  and and_2 (and_2_out, not_1_out, not_3_out, not_2_out, W);
  and and_3 (and_3_out, not_1_out, M);
  or or_1 (A1, and_1_out, and_2_out);
  or or_2 (A0, and_3_out, and_2_out);

  assign A2 = F;

  // Notes on the sheet:
  //   Summer 2023
endmodule

module Fall23 (
  input  P,
  input  C,
  input  L,
  input  Q,
  input  A,
  output A2,
  output A1,
  output A0
);

  wire and_1_out, and_2_out, and_3_out, and_4_out, and_5_out, not_1_out, not_2_out, not_3_out, not_4_out,
       not_5_out;

  not not_1 (not_1_out, P);
  not not_2 (not_2_out, C);
  not not_3 (not_3_out, L);
  not not_4 (not_4_out, Q);
  not not_5 (not_5_out, A);
  and and_1 (and_1_out, not_1_out, not_2_out, L);
  and and_2 (and_2_out, not_1_out, not_2_out, not_3_out, not_4_out, A);
  and and_3 (and_3_out, not_1_out, C);
  and and_4 (and_4_out, not_1_out, not_2_out, L);
  and and_5 (and_5_out, not_1_out, not_2_out, not_3_out, Q);
  or or_1 (A2, and_1_out, and_2_out);
  or or_2 (A1, and_2_out, and_3_out, P, and_4_out);
  or or_3 (A0, and_3_out, and_4_out, and_5_out);

  // Notes on the sheet:
  //   Fall 2023
endmodule

module Fall18 (
  input  D1,
  input  D2,
  input  D0,
  input  D3,
  output Y1,
  output Y0
);

  wire and_1_out, and_2_out, not_1_out, not_2_out, not_3_out, not_4_out;

  not not_1 (not_1_out, D1);
  not not_2 (not_2_out, D0);
  not not_3 (not_3_out, D2);
  not not_4 (not_4_out, D3);
  and and_1 (and_1_out, not_1_out, D2);
  and and_2 (and_2_out, not_1_out, not_3_out, not_2_out, D3);
  or or_1 (Y1, and_1_out, and_2_out);
  or or_2 (Y0, and_2_out, D1);

  // Notes on the sheet:
  //   Fall 2018
endmodule

module Summer2019 (
  input  F,
  input  B,
  input  S,
  input  D,
  input  W,
  output A2,
  output A1,
  output A0
);

  wire and_1_out, and_2_out, and_3_out, and_4_out, not_1_out, not_2_out, not_3_out, not_4_out, not_5_out;

  not not_1 (not_1_out, F);
  not not_2 (not_2_out, B);
  not not_3 (not_3_out, S);
  not not_4 (not_4_out, D);
  not not_5 (not_5_out, W);
  and and_1 (and_1_out, not_1_out, B);
  and and_2 (and_2_out, not_1_out, not_2_out, S);
  and and_3 (and_3_out, not_1_out, not_2_out, not_3_out, D);
  and and_4 (and_4_out, not_1_out, not_2_out, not_3_out, not_4_out, W);
  or or_1 (A2, and_1_out, and_2_out);
  or or_2 (A1, and_2_out, F, and_3_out);
  or or_3 (A0, F, and_2_out, and_4_out);

  // Notes on the sheet:
  //   Summer 2019
endmodule

module Fall19 (
  input  D0,
  input  D1,
  input  D3,
  input  D2,
  output Y1,
  output Y0
);

  wire and_1_out, and_2_out, and_3_out, and_4_out, not_1_out, not_2_out, not_3_out, not_4_out;

  not not_1 (not_1_out, D0);
  not not_2 (not_2_out, D3);
  not not_3 (not_3_out, D1);
  not not_4 (not_4_out, D2);
  and and_1 (and_1_out, not_1_out, not_3_out, D3);
  and and_2 (and_2_out, not_1_out, not_3_out, not_2_out, D2);
  and and_3 (and_3_out, not_1_out, D1);
  and and_4 (and_4_out, not_1_out, not_3_out, D3);
  or or_1 (Y1, and_1_out, and_2_out);
  or or_2 (Y0, and_3_out, and_4_out);

  // Notes on the sheet:
  //   Fall2019
endmodule

module Spring2020 (
  input  F,
  input  W,
  input  B,
  input  S,
  input  D,
  output A2,
  output A1,
  output A0
);

  wire and_1_out, and_2_out, and_3_out, and_4_out, not_1_out, not_2_out, not_3_out, not_4_out, not_5_out;

  not not_1 (not_1_out, F);
  not not_2 (not_2_out, B);
  not not_3 (not_3_out, W);
  not not_4 (not_4_out, S);
  not not_5 (not_5_out, D);
  and and_1 (and_1_out, not_1_out, W);
  and and_2 (and_2_out, not_1_out, not_3_out, B);
  and and_3 (and_3_out, not_1_out, not_3_out, not_2_out, S);
  and and_4 (and_4_out, not_1_out, not_3_out, not_2_out, not_4_out, D);
  or or_1 (A2, and_1_out, and_2_out, and_3_out);
  or or_2 (A1, and_1_out, and_3_out, and_4_out);
  or or_3 (A0, and_2_out, and_4_out, and_3_out, F);

  // Notes on the sheet:
  //   Spring 2020
endmodule

module Summer2020 (
  input  D1,
  input  D3,
  input  D0,
  input  D2,
  output Y1,
  output Y0
);

  wire and_1_out, and_2_out, not_1_out, not_2_out, not_3_out, not_4_out;

  not not_1 (not_1_out, D1);
  not not_2 (not_2_out, D0);
  not not_3 (not_3_out, D3);
  not not_4 (not_4_out, D2);
  and and_1 (and_1_out, not_1_out, D3);
  and and_2 (and_2_out, not_1_out, not_3_out, not_2_out, D2);
  or or_1 (Y1, and_1_out, and_2_out);
  or or_2 (Y0, and_1_out, D1);
endmodule

module Fall2020 (
  input  F,
  input  S,
  input  B,
  input  W,
  input  D,
  output A2,
  output A1,
  output A0
);

  wire and_2_out, and_3_out, not_1_out, not_2_out, not_3_out, not_4_out, not_5_out;

  not not_1 (not_1_out, F);
  not not_2 (not_2_out, B);
  not not_3 (not_3_out, S);
  not not_4 (not_4_out, W);
  not not_5 (not_5_out, D);
  and and_1 (A1, not_1_out, S);
  and and_2 (and_2_out, not_1_out, not_3_out, B);
  and and_3 (and_3_out, not_1_out, not_3_out, not_2_out, W);
  or or_1 (A0, A1, and_3_out, F);
  or or_2 (A2, A1, and_2_out, and_3_out);

  // Notes on the sheet:
  //   Fall 2022
endmodule

module Spring2021 (
  input  F,
  input  K,
  input  T,
  input  E,
  input  U,
  input  S,
  output A2,
  output A1,
  output A0
);

  wire and_1_out, and_2_out, and_3_out, and_4_out, and_5_out, not_1_out, not_2_out, not_3_out, not_4_out,
       not_5_out, not_6_out;

  not not_1 (not_1_out, F);
  not not_2 (not_2_out, K);
  not not_3 (not_3_out, E);
  not not_4 (not_4_out, T);
  not not_5 (not_5_out, U);
  not not_6 (not_6_out, S);
  and and_1 (and_1_out, not_1_out, K);
  and and_2 (and_2_out, not_1_out, not_2_out, T);
  and and_3 (and_3_out, not_1_out, not_2_out, not_4_out, E);
  and and_4 (and_4_out, not_1_out, not_2_out, not_4_out, not_3_out, U);
  and and_5 (and_5_out, not_1_out, not_2_out, not_4_out, not_3_out, not_5_out, S);
  or or_1 (A0, and_1_out, and_3_out, and_2_out, F);
  or or_2 (A2, and_1_out, and_4_out, and_2_out);
  or or_3 (A1, and_3_out, and_1_out, and_5_out);

  // Notes on the sheet:
  //   Spring 2021
endmodule

module spring2024 (
  input  N,
  input  I,
  input  O,
  input  M,
  input  G,
  output A2,
  output A1,
  output A0
);

  wire and_1_out, and_2_out, and_3_out, and_4_out, and_5_out, not_1_out, not_2_out, not_3_out, not_4_out,
       not_5_out;

  not not_1 (not_1_out, N);
  not not_2 (not_2_out, I);
  not not_3 (not_3_out, O);
  not not_4 (not_4_out, M);
  not not_5 (not_5_out, G);
  and and_1 (and_1_out, not_1_out, not_2_out, not_3_out, M);
  and and_2 (and_2_out, not_1_out, not_2_out, not_3_out, not_4_out, G);
  and and_3 (and_3_out, not_1_out, not_2_out, O);
  and and_4 (and_4_out, not_1_out, I);
  and and_5 (and_5_out, not_1_out, not_2_out, not_3_out, M);
  or or_1 (A2, N, and_4_out, and_5_out);
  or or_2 (A1, and_4_out, and_1_out, and_2_out);
  or or_3 (A0, and_3_out, and_4_out);
endmodule
