// Logisim project SyncronousupdounDff.circ as structural Verilog: 2 circuits, main circuit main
module main (
  input  Reset,
  output Up_count,
  output out_3,
  output out_4,
  output out_5,
  output out_6,
  output out_7
);

  wire and_1_out, and_2_out, and_3_out, and_4_out, and_5_out, clock_1_out, or_1_out, or_2_out;

  or or_1 (or_1_out, and_1_out, and_2_out, and_3_out);
  or or_2 (or_2_out, and_4_out, and_5_out);
  Clock clock_1 (.out(clock_1_out));
  and and_1 (and_1_out, out_6, out_4, out_3);
  and and_2 (and_2_out, out_7, Up_count);
  and and_3 (and_3_out, out_5, Up_count);
  and and_4 (and_4_out, out_5, out_6);
  and and_5 (and_5_out, out_4, out_7);
  D_Flip_Flop #(.trigger("falling")) Q2 (
    .clk(clock_1_out), .D(or_1_out), .Q(Up_count), .Qn(out_3), .en(1'b1), .reset(Reset));  // open: preset
  D_Flip_Flop #(.trigger("falling")) Q1 (
    .clk(clock_1_out), .D(or_2_out), .Q(out_4), .Qn(out_5), .en(1'b1), .reset(Reset));  // open: preset
  D_Flip_Flop #(.trigger("falling")) Q0 (
    .clk(clock_1_out), .D(out_7), .Q(out_6), .Qn(out_7), .en(1'b1), .reset(Reset));  // open: preset

  // Notes on the sheet:
  //   Down count
endmodule

module down (
  input  Reset,
  output Down_count,
  output out_3,
  output out_4,
  output out_5,
  output out_6,
  output out_7
);

  wire and_1_out, and_2_out, and_3_out, and_4_out, and_5_out, clock_1_out, or_1_out, or_2_out;

  or or_1 (or_1_out, and_1_out, and_2_out, and_3_out);
  or or_2 (or_2_out, and_4_out, and_5_out);
  Clock clock_1 (.out(clock_1_out));
  and and_1 (and_1_out, out_7, out_5, out_3);
  and and_2 (and_2_out, out_4, Down_count);
  and and_3 (and_3_out, out_6, Down_count);
  and and_4 (and_4_out, out_5, out_7);
  and and_5 (and_5_out, out_4, out_6);
  D_Flip_Flop #(.trigger("falling")) Q2 (
    .clk(clock_1_out), .D(or_1_out), .Q(Down_count), .Qn(out_3), .en(1'b1), .reset(Reset));  // open: preset
  D_Flip_Flop #(.trigger("falling")) Q1 (
    .clk(clock_1_out), .D(or_2_out), .Q(out_4), .Qn(out_5), .en(1'b1), .reset(Reset));  // open: preset
  D_Flip_Flop #(.trigger("falling")) Q0 (
    .clk(clock_1_out), .D(out_7), .Q(out_6), .Qn(out_7), .en(1'b1), .reset(Reset));  // open: preset

  // Notes on the sheet:
  //   Up count
endmodule
