// Logisim project SyncronousupdownuseT.circ as structural Verilog: 2 circuits, main circuit main
module main (
  input  reset,
  output up,
  output down,
  output out_4,
  output out_5,
  output out_6,
  output out_7
);

  wire and_1_out, clock_1_out;

  Clock clock_1 (.out(clock_1_out));
  T_Flip_Flop t_ff_1 (.clk(clock_1_out), .T(and_1_out), .Q(up), .Qn(down), .reset(reset), .en(1'b1));  // open: preset
  T_Flip_Flop t_ff_2 (.clk(clock_1_out), .T(out_6), .Q(out_4), .Qn(out_5), .reset(reset), .en(1'b1));  // open: preset
  T_Flip_Flop t_ff_3 (.clk(clock_1_out), .T(1'b1), .Q(out_6), .Qn(out_7), .reset(reset), .en(1'b1));  // open: preset
  and and_1 (and_1_out, out_4, out_6);
endmodule

module down (
  input  reset,
  output down,
  output up,
  output out_4,
  output out_5,
  output out_6,
  output out_7
);

  wire and_1_out, clock_1_out;

  Clock clock_1 (.out(clock_1_out));
  T_Flip_Flop t_ff_1 (.clk(clock_1_out), .T(and_1_out), .Q(down), .Qn(up), .reset(reset), .en(1'b1));  // open: preset
  T_Flip_Flop t_ff_2 (.clk(clock_1_out), .T(out_7), .Q(out_4), .Qn(out_5), .reset(reset), .en(1'b1));  // open: preset
  T_Flip_Flop t_ff_3 (.clk(clock_1_out), .T(1'b1), .Q(out_6), .Qn(out_7), .reset(reset), .en(1'b1));  // open: preset
  and and_1 (and_1_out, out_5, out_7);
endmodule
