// Logisim project arbitary_counter.circ as structural Verilog
module spring2024 (
  output A2,
  output A1,
  output A0
);

  wire and_1_out, and_2_out, and_3_out, and_4_out, and_5_out, and_6_out, and_7_out, clock_1_out, or_1_out,
       or_2_out, or_3_out, Q0_qn, Q1_qn, Q2_qn;

  Clock clock_1 (.out(clock_1_out));
  and and_1 (and_1_out, Q2_qn, A0);
  and and_2 (and_2_out, Q2_qn, A1);
  and and_3 (and_3_out, Q1_qn, A0);
  and and_4 (and_4_out, A2, A1, Q0_qn);
  and and_5 (and_5_out, Q1_qn, Q0_qn);
  and and_6 (and_6_out, A2, A0);
  and and_7 (and_7_out, Q2_qn, Q0_qn);
  or or_1 (or_1_out, and_1_out, and_2_out);
  or or_2 (or_2_out, and_5_out, and_6_out, and_7_out);
  or or_3 (or_3_out, and_3_out, and_4_out);
  D_Flip_Flop #(.trigger("falling")) Q2 (
    .clk(clock_1_out), .D(or_1_out), .Q(A2), .Qn(Q2_qn), .en(1'b1));  // open: preset, reset
  D_Flip_Flop #(.trigger("falling")) Q1 (
    .clk(clock_1_out), .D(or_3_out), .Q(A1), .Qn(Q1_qn), .en(1'b1));  // open: preset, reset
  D_Flip_Flop #(.trigger("falling")) Q0 (
    .clk(clock_1_out), .D(or_2_out), .Q(A0), .Qn(Q0_qn), .en(1'b1));  // open: preset, reset
endmodule

module fall2023 (
  output A2,
  output A1,
  output A0
);

  wire and_1_out, and_2_out, and_3_out, and_4_out, clock_1_out, j_k_ff_1_qn, j_k_ff_2_qn, j_k_ff_3_qn;

  Clock clock_1 (.out(clock_1_out));
  and and_1 (and_1_out, A1, j_k_ff_3_qn);
  and and_2 (and_2_out, j_k_ff_2_qn, A0);
  and and_3 (and_3_out, A2, A1);
  and and_4 (and_4_out, j_k_ff_1_qn, j_k_ff_2_qn);
  J_K_Flip_Flop j_k_ff_1 (
    .J(and_1_out), .clk(clock_1_out), .K(and_2_out), .Q(A2), .Qn(j_k_ff_1_qn), .en(1'b1));  // open: preset, reset
  J_K_Flip_Flop j_k_ff_2 (
    .J(1'b1), .clk(clock_1_out), .K(1'b1), .Q(A1), .Qn(j_k_ff_2_qn), .en(1'b1));  // open: preset, reset
  J_K_Flip_Flop j_k_ff_3 (
    .J(and_3_out), .clk(clock_1_out), .K(and_4_out), .Q(A0), .Qn(j_k_ff_3_qn), .en(1'b1));  // open: preset, reset
endmodule

module spring2023 (
  output A2,
  output A1,
  output A0
);

  wire and_1_out, and_2_out, and_3_out, and_4_out, and_5_out, clock_1_out, or_1_out, or_2_out, or_3_out,
       t_ff_1_qn, t_ff_2_qn, t_ff_3_qn;

  Clock clock_1 (.out(clock_1_out));
  and and_1 (and_1_out, A1, A0);
  and and_2 (and_2_out, t_ff_1_qn, A1);
  and and_3 (and_3_out, t_ff_1_qn, A0);
  and and_4 (and_4_out, A2, A1);
  and and_5 (and_5_out, A2, t_ff_3_qn);
  or or_1 (or_1_out, and_1_out, and_2_out);
  or or_2 (or_2_out, t_ff_1_qn, A0);
  or or_3 (or_3_out, and_3_out, and_4_out, and_5_out);
  T_Flip_Flop #(.trigger("falling")) t_ff_1 (
    .clk(clock_1_out), .T(or_1_out), .Q(A2), .Qn(t_ff_1_qn));  // open: preset, reset, en
  T_Flip_Flop #(.trigger("falling")) t_ff_2 (
    .clk(clock_1_out), .T(or_2_out), .Q(A1), .Qn(t_ff_2_qn));  // open: preset, reset, en
  T_Flip_Flop #(.trigger("falling")) t_ff_3 (
    .clk(clock_1_out), .T(or_3_out), .Q(A0), .Qn(t_ff_3_qn));  // open: preset, reset, en
endmodule
