// Logisim project mux.circ as structural Verilog: 21 circuits, main circuit main
module main (
  input  _0,
  input  _1,
  input  _2,
  input  _3,
  input  S3,
  input  S2,
  input  S1,
  input  S0,
  input  _4,
  input  _5,
  input  _6,
  input  _7,
  input  _8,
  input  _9,
  input  _10,
  input  _11,
  input  _12,
  input  _13,
  input  _14,
  input  _15,
  output out_21
);

  wire multiplexer_1_out, multiplexer_2_out, multiplexer_3_out, multiplexer_4_out, multiplexer_5_out,
       multiplexer_6_out, multiplexer_7_out, multiplexer_8_out, multiplexer_9_out, multiplexer_10_out,
       multiplexer_11_out, multiplexer_12_out, multiplexer_13_out, multiplexer_14_out;

  Multiplexer #(.disabled(0)) multiplexer_1 (.in0(_0), .in1(_1), .out(multiplexer_1_out), .sel(S0), .en(1'b1));
  Multiplexer #(.disabled(0)) multiplexer_2 (.in0(_2), .in1(_3), .out(multiplexer_2_out), .sel(S0), .en(1'b1));
  Multiplexer #(.disabled(0)) multiplexer_3 (.in0(_4), .in1(_5), .out(multiplexer_3_out), .sel(S0), .en(1'b1));
  Multiplexer #(.disabled(0)) multiplexer_4 (.in0(_6), .in1(_7), .out(multiplexer_4_out), .sel(S0), .en(1'b1));
  Multiplexer #(.disabled(0)) multiplexer_5 (.in0(_8), .in1(_9), .out(multiplexer_5_out), .sel(S0), .en(1'b1));
  Multiplexer #(.disabled(0)) multiplexer_6 (.in0(_10), .in1(_11), .out(multiplexer_6_out), .sel(S0), .en(1'b1));
  Multiplexer #(.disabled(0)) multiplexer_7 (.in0(_12), .in1(_13), .out(multiplexer_7_out), .sel(S0), .en(1'b1));
  Multiplexer #(.disabled(0)) multiplexer_8 (.in0(_14), .in1(_15), .out(multiplexer_8_out), .sel(S0), .en(1'b1));
  Multiplexer #(.disabled(0)) multiplexer_9 (
    .in0(multiplexer_1_out), .in1(multiplexer_2_out), .out(multiplexer_9_out), .sel(S1), .en(1'b1));
  Multiplexer #(.disabled(0)) multiplexer_10 (
    .in0(multiplexer_3_out), .in1(multiplexer_4_out), .out(multiplexer_10_out), .sel(S1), .en(1'b1));
  Multiplexer #(.disabled(0)) multiplexer_11 (
    .in0(multiplexer_5_out), .in1(multiplexer_6_out), .out(multiplexer_11_out), .sel(S1), .en(1'b1));
  Multiplexer #(.disabled(0)) multiplexer_12 (
    .in0(multiplexer_7_out), .in1(multiplexer_8_out), .out(multiplexer_12_out), .sel(S1), .en(1'b1));
  Multiplexer #(.disabled(0)) multiplexer_13 (
    .in0(multiplexer_9_out), .in1(multiplexer_10_out), .out(multiplexer_13_out), .sel(S2), .en(1'b1));
  Multiplexer #(.disabled(0)) multiplexer_14 (
    .in0(multiplexer_11_out), .in1(multiplexer_12_out), .out(multiplexer_14_out), .sel(S2), .en(1'b1));
  Multiplexer #(.disabled(0)) multiplexer_15 (
    .in0(multiplexer_13_out), .in1(multiplexer_14_out), .out(out_21), .sel(S3), .en(1'b1));
endmodule

module _16_1_use_2_1 (
  input  _0,
  input  _1,
  input  _2,
  input  _3,
  input  S3,
  input  S2,
  input  S1,
  input  S0,
  input  _4,
  input  _5,
  input  _6,
  input  _7,
  input  _8,
  input  _9,
  input  _10,
  input  _11,
  input  _12,
  input  _13,
  input  _14,
  input  _15,
  output out_21
);

  wire multiplexer_1_out, multiplexer_2_out, multiplexer_3_out, multiplexer_4_out, multiplexer_5_out,
       multiplexer_6_out, multiplexer_7_out, multiplexer_8_out, multiplexer_9_out, multiplexer_10_out,
       multiplexer_11_out, multiplexer_12_out, multiplexer_13_out, multiplexer_14_out;

  Multiplexer #(.disabled(0)) multiplexer_1 (.in0(_0), .in1(_1), .out(multiplexer_1_out), .sel(S0), .en(1'b1));
  Multiplexer #(.disabled(0)) multiplexer_2 (.in0(_2), .in1(_3), .out(multiplexer_2_out), .sel(S0), .en(1'b1));
  Multiplexer #(.disabled(0)) multiplexer_3 (.in0(_4), .in1(_5), .out(multiplexer_3_out), .sel(S0), .en(1'b1));
  Multiplexer #(.disabled(0)) multiplexer_4 (.in0(_6), .in1(_7), .out(multiplexer_4_out), .sel(S0), .en(1'b1));
  Multiplexer #(.disabled(0)) multiplexer_5 (.in0(_8), .in1(_9), .out(multiplexer_5_out), .sel(S0), .en(1'b1));
  Multiplexer #(.disabled(0)) multiplexer_6 (.in0(_10), .in1(_11), .out(multiplexer_6_out), .sel(S0), .en(1'b1));
  Multiplexer #(.disabled(0)) multiplexer_7 (.in0(_12), .in1(_13), .out(multiplexer_7_out), .sel(S0), .en(1'b1));
  Multiplexer #(.disabled(0)) multiplexer_8 (.in0(_14), .in1(_15), .out(multiplexer_8_out), .sel(S0), .en(1'b1));
  Multiplexer #(.disabled(0)) multiplexer_9 (
    .in0(multiplexer_1_out), .in1(multiplexer_2_out), .out(multiplexer_9_out), .sel(S1), .en(1'b1));
  Multiplexer #(.disabled(0)) multiplexer_10 (
    .in0(multiplexer_3_out), .in1(multiplexer_4_out), .out(multiplexer_10_out), .sel(S1), .en(1'b1));
  Multiplexer #(.disabled(0)) multiplexer_11 (
    .in0(multiplexer_5_out), .in1(multiplexer_6_out), .out(multiplexer_11_out), .sel(S1), .en(1'b1));
  Multiplexer #(.disabled(0)) multiplexer_12 (
    .in0(multiplexer_7_out), .in1(multiplexer_8_out), .out(multiplexer_12_out), .sel(S1), .en(1'b1));
  Multiplexer #(.disabled(0)) multiplexer_13 (
    .in0(multiplexer_9_out), .in1(multiplexer_10_out), .out(multiplexer_13_out), .sel(S2), .en(1'b1));
  Multiplexer #(.disabled(0)) multiplexer_14 (
    .in0(multiplexer_11_out), .in1(multiplexer_12_out), .out(multiplexer_14_out), .sel(S2), .en(1'b1));
  Multiplexer #(.disabled(0)) multiplexer_15 (
    .in0(multiplexer_13_out), .in1(multiplexer_14_out), .out(out_21), .sel(S3), .en(1'b1));
endmodule

module all_mux (
  input  in_1,
  input  _0,
  input  _1,
  input  in_4,
  input  Select,
  input  _2,
  input  _4,
  input  _4_2,
  input  _0_2,
  input  _5,
  input  _1_2,
  input  _6,
  input  _7,
  input  _8,
  input  _2_2,
  input  _9,
  input  _3,
  input  _10,
  input  _11,
  input  [1:0] Select_2,
  input  _12,
  input  _13,
  input  _14,
  input  _15,
  input  [3:0] Select_3,
  input  _0_3,
  input  _1_3,
  input  _2_3,
  input  _4_3,
  input  _4_4,
  input  _5_2,
  input  _6_2,
  input  _7_2,
  input  [2:0] Select_4,
  output out_35,
  output out_36,
  output out_37,
  output out_38
);

  Multiplexer #(.disabled(0)) multiplexer_1 (.in0(in_1), .in1(in_4), .out(out_35), .sel(Select), .en(1'b1));
  Multiplexer #(.select(2), .disabled(0)) multiplexer_2 (
    .in0(_0_2), .in1(_1_2), .in2(_2_2), .in3(_3), .out(out_37), .sel(Select_2), .en(1'b1));
  Multiplexer #(.select(3), .disabled(0)) multiplexer_3 (
    .in0(_0_3), .in1(_1_3), .in2(_2_3), .in3(_4_3), .in4(_4_4), .in5(_5_2), .in6(_6_2), .in7(_7_2),
    .out(out_38), .sel(Select_4), .en(1'b1));
  Multiplexer #(.select(4)) multiplexer_4 (
    .in0(_0), .in1(_1), .in2(_2), .in3(_4), .in4(_4_2), .in5(_5), .in6(_6), .in7(_7), .in8(_8), .in9(_9),
    .in10(_10), .in11(_11), .in12(_12), .in13(_13), .in14(_14), .in15(_15), .out(out_36), .sel(Select_3),
    .en(1'b1));

  // Notes on the sheet:
  //   4 to 1 mux
  //   2 to1 mux
  //   8 to 1 mux
  //   16 t0 1 mux
endmodule

module _4_to_1_use_2_1 (
  input  in_1,
  input  in_2,
  input  in_3,
  input  in_4,
  input  in_5,
  input  in_6,
  output out_7
);

  wire multiplexer_1_out, multiplexer_2_out;

  Multiplexer #(.disabled(0), .enable("false")) multiplexer_1 (
    .in0(in_3), .in1(in_4), .out(multiplexer_1_out), .sel(in_2));
  Multiplexer #(.disabled(0), .enable("false")) multiplexer_2 (
    .in0(in_5), .in1(in_6), .out(multiplexer_2_out), .sel(in_2));
  Multiplexer #(.disabled(0), .enable("false")) multiplexer_3 (
    .in0(multiplexer_1_out), .in1(multiplexer_2_out), .out(out_7), .sel(in_1));
endmodule

module _8_t0_1use2_to_1 (
  input  A,
  input  B,
  input  C,
  input  _0,
  input  _1,
  input  _2,
  input  _3,
  input  _4,
  input  _5,
  input  _6,
  input  _7,
  output out_12
);

  wire multiplexer_1_out, multiplexer_2_out, multiplexer_3_out, multiplexer_4_out, multiplexer_5_out,
       multiplexer_6_out;

  Multiplexer #(.disabled(0), .enable("false")) multiplexer_1 (.in0(_0), .in1(_1), .out(multiplexer_1_out), .sel(C));
  Multiplexer #(.disabled(0), .enable("false")) multiplexer_2 (.in0(_2), .in1(_3), .out(multiplexer_2_out), .sel(C));
  Multiplexer #(.disabled(0), .enable("false")) multiplexer_3 (.in0(_4), .in1(_5), .out(multiplexer_3_out), .sel(C));
  Multiplexer #(.disabled(0), .enable("false")) multiplexer_4 (.in0(_6), .in1(_7), .out(multiplexer_4_out), .sel(C));
  Multiplexer #(.disabled(0), .enable("false")) multiplexer_5 (
    .in0(multiplexer_1_out), .in1(multiplexer_2_out), .out(multiplexer_5_out), .sel(B));
  Multiplexer #(.disabled(0), .enable("false")) multiplexer_6 (
    .in0(multiplexer_3_out), .in1(multiplexer_4_out), .out(multiplexer_6_out), .sel(B));
  Multiplexer #(.disabled(0), .enable("false")) multiplexer_7 (
    .in0(multiplexer_5_out), .in1(multiplexer_6_out), .out(out_12), .sel(A));
endmodule

module _16_to_1_use_4_t0_1 (
  input  A,
  input  B,
  input  C,
  input  D,
  input  _0,
  input  in_6,
  input  in_7,
  input  _3,
  input  _4,
  input  in_10,
  input  in_11,
  input  _7,
  input  _8,
  input  in_14,
  input  in_15,
  input  _11,
  input  in_17,
  input  in_18,
  input  in_19,
  input  _15,
  output out_21
);

  wire multiplexer_1_out, multiplexer_2_out, multiplexer_3_out, multiplexer_4_out;

  Multiplexer #(.select(2), .disabled(0), .enable("false")) multiplexer_1 (
    .in0(_0), .in1(in_6), .in2(in_7), .in3(_3), .out(multiplexer_1_out), .sel({C, D}));
  Multiplexer #(.select(2), .disabled(0), .enable("false")) multiplexer_2 (
    .in0(_4), .in1(in_10), .in2(in_11), .in3(_7), .out(multiplexer_2_out), .sel({C, D}));
  Multiplexer #(.select(2), .disabled(0), .enable("false")) multiplexer_3 (
    .in0(_8), .in1(in_14), .in2(in_15), .in3(_11), .out(multiplexer_3_out), .sel({C, D}));
  Multiplexer #(.select(2), .disabled(0), .enable("false")) multiplexer_4 (
    .in0(in_17), .in1(in_18), .in2(in_19), .in3(_15), .out(multiplexer_4_out), .sel({C, D}));
  Multiplexer #(.select(2), .disabled(0), .enable("false")) multiplexer_5 (
    .in0(multiplexer_1_out), .in1(multiplexer_2_out), .in2(multiplexer_3_out), .in3(multiplexer_4_out),
    .out(out_21), .sel({A, B}));
endmodule

module fall2023 (
  input  A,
  input  B,
  input  C,
  input  D,
  output out_5
);

  wire and_1_out, not_1_out, not_2_out, or_1_out, xor_1_out;

  not not_1 (not_1_out, C);
  not not_2 (not_2_out, D);
  and and_1 (and_1_out, not_1_out, not_2_out);
  or or_1 (or_1_out, not_1_out, not_2_out);
  xor xor_1 (xor_1_out, C, D);
  Multiplexer #(.select(2), .disabled(0), .enable("false")) multiplexer_1 (
    .in0(and_1_out), .in1(C), .in2(or_1_out), .in3(xor_1_out), .out(out_5), .sel({A, B}));
endmodule

module spring2023 (
  input  A,
  input  B,
  input  C,
  input  D,
  output out_5
);

  wire and_1_out, not_1_out, not_2_out, or_1_out;

  not not_1 (not_1_out, D);
  not not_2 (not_2_out, C);
  and and_1 (and_1_out, not_2_out, D);
  or or_1 (or_1_out, C, D);
  Multiplexer #(.select(2), .disabled(0), .enable("false")) multiplexer_1 (
    .in0(D), .in1(D), .in2(and_1_out), .in3(or_1_out), .out(out_5), .sel({A, B}));
endmodule

module fall2022 (
  input  A,
  input  B,
  input  C,
  input  D,
  output out_5
);

  wire and_1_out, not_1_out, not_2_out;

  not not_1 (not_1_out, D);
  not not_2 (not_2_out, C);
  and and_1 (and_1_out, not_2_out, D);
  Multiplexer #(.select(2), .disabled(0), .enable("false")) multiplexer_1 (
    .in0(not_2_out), .in1(not_1_out), .in2(and_1_out), .in3(not_1_out), .out(out_5), .sel({A, B}));
endmodule

module summer2022 (
  input  A,
  input  B,
  input  C,
  input  D,
  output out_5
);

  wire and_1_out, not_1_out, not_2_out, or_1_out, or_2_out;

  not not_1 (not_1_out, D);
  not not_2 (not_2_out, C);
  or or_1 (or_1_out, not_2_out, D);
  or or_2 (or_2_out, C, not_1_out);
  and and_1 (and_1_out, C, not_1_out);
  Multiplexer #(.select(2), .disabled(0), .enable("false")) multiplexer_1 (
    .in0(or_1_out), .in1(or_2_out), .in2(and_1_out), .in3(1'b1), .out(out_5), .sel({A, B}));
endmodule

module spring2022 (
  input  A,
  input  B,
  input  C,
  input  D,
  output out_5
);

  wire not_1_out;

  not not_1 (not_1_out, D);
  Multiplexer #(.select(3), .disabled(0), .enable("false")) multiplexer_1 (
    .in0(1'b1), .in1(not_1_out), .in2(not_1_out), .in3(1'b0), .in4(not_1_out), .in5(1'b0), .in6(1'b0),
    .in7(1'b0), .out(out_5), .sel({A, B, C}));
endmodule

module fall21 (
  input  W,
  input  X,
  input  Y,
  input  Z,
  output out_5
);

  wire not_1_out;

  not not_1 (not_1_out, Z);
  Multiplexer #(.select(3), .disabled(0), .enable("false")) multiplexer_1 (
    .in0(Z), .in1(Z), .in2(not_1_out), .in3(1'b0), .in4(1'b0), .in5(Z), .in6(1'b1), .in7(1'b1), .out(out_5),
    .sel({W, X, Y}));
endmodule

module summer21 (
  input  A,
  input  B,
  input  C,
  output out_4
);

  wire multiplexer_1_out, multiplexer_2_out, multiplexer_3_out, multiplexer_4_out, multiplexer_5_out,
       multiplexer_6_out;

  Multiplexer #(.disabled(0), .enable("false")) multiplexer_1 (
    .in0(1'b1), .in1(1'b1), .out(multiplexer_1_out), .sel(C));
  Multiplexer #(.disabled(0), .enable("false")) multiplexer_2 (
    .in0(1'b1), .in1(1'b0), .out(multiplexer_2_out), .sel(C));
  Multiplexer #(.disabled(0), .enable("false")) multiplexer_3 (
    .in0(1'b1), .in1(1'b0), .out(multiplexer_3_out), .sel(C));
  Multiplexer #(.disabled(0), .enable("false")) multiplexer_4 (
    .in0(1'b0), .in1(1'b0), .out(multiplexer_4_out), .sel(C));
  Multiplexer #(.disabled(0), .enable("false")) multiplexer_5 (
    .in0(multiplexer_1_out), .in1(multiplexer_2_out), .out(multiplexer_5_out), .sel(B));
  Multiplexer #(.disabled(0), .enable("false")) multiplexer_6 (
    .in0(multiplexer_3_out), .in1(multiplexer_4_out), .out(multiplexer_6_out), .sel(B));
  Multiplexer #(.disabled(0), .enable("false")) multiplexer_7 (
    .in0(multiplexer_5_out), .in1(multiplexer_6_out), .out(out_4), .sel(A));
endmodule

module spring2021 (
  input  A,
  input  B,
  input  C,
  output out_4
);

  wire not_1_out, xnor_1_out;

  not not_1 (not_1_out, C);
  xnor xnor_1 (xnor_1_out, B, C);
  Multiplexer #(.disabled(0), .enable("false")) multiplexer_1 (.in0(not_1_out), .in1(xnor_1_out), .out(out_4), .sel(A));
endmodule

module spring2021_2 (
  input  A,
  input  B,
  input  C,
  input  D,
  output out_5
);

  wire multiplexer_1_out, multiplexer_2_out, multiplexer_3_out, multiplexer_4_out;

  Multiplexer #(.select(2), .disabled(0), .enable("false")) multiplexer_1 (
    .in0(1'b1), .in1(1'b1), .in2(1'b1), .in3(1'b0), .out(multiplexer_1_out), .sel({C, D}));
  Multiplexer #(.select(2), .disabled(0), .enable("false")) multiplexer_2 (
    .in0(1'b1), .in1(1'b0), .in2(1'b0), .in3(1'b1), .out(multiplexer_2_out), .sel({C, D}));
  Multiplexer #(.select(2), .disabled(0), .enable("false")) multiplexer_3 (
    .in0(1'b1), .in1(1'b0), .in2(1'b0), .in3(1'b1), .out(multiplexer_3_out), .sel({C, D}));
  Multiplexer #(.select(2), .disabled(0), .enable("false")) multiplexer_4 (
    .in0(1'b0), .in1(1'b1), .in2(1'b1), .in3(1'b1), .out(multiplexer_4_out), .sel({C, D}));
  Multiplexer #(.select(2), .disabled(0), .enable("false")) multiplexer_5 (
    .in0(multiplexer_1_out), .in1(multiplexer_2_out), .in2(multiplexer_3_out), .in3(multiplexer_4_out),
    .out(out_5), .sel({A, B}));
endmodule

module fall2020 (
  input  A,
  input  B,
  input  C,
  input  D,
  output out_5
);

  wire and_1_out, and_2_out, not_1_out, not_2_out, or_1_out, xnor_1_out;

  not not_1 (not_1_out, C);
  not not_2 (not_2_out, D);
  xnor xnor_1 (xnor_1_out, C, D);
  and and_1 (and_1_out, C, not_2_out);
  and and_2 (and_2_out, not_1_out, not_2_out);
  or or_1 (or_1_out, C, not_2_out);
  Multiplexer #(.select(2), .disabled(0), .enable("false")) multiplexer_1 (
    .in0(xnor_1_out), .in1(and_1_out), .in2(and_2_out), .in3(or_1_out), .out(out_5), .sel({A, B}));
endmodule

module summer2020 (
  input  A,
  input  B,
  input  C,
  input  D,
  output out_5
);

  wire not_1_out;

  not not_1 (not_1_out, D);
  Multiplexer #(.select(3), .disabled(0), .enable("false")) multiplexer_1 (
    .in0(D), .in1(1'b0), .in2(1'b1), .in3(not_1_out), .in4(not_1_out), .in5(1'b1), .in6(not_1_out),
    .in7(1'b0), .out(out_5), .sel({A, B, C}));
endmodule

module spring2020 (
  input  A,
  input  B,
  input  C,
  input  D,
  output out_5
);

  wire and_1_out, not_1_out, not_2_out;

  not not_1 (not_1_out, C);
  not not_2 (not_2_out, D);
  and and_1 (and_1_out, not_1_out, D);
  Multiplexer #(.select(2), .disabled(0), .enable("false")) multiplexer_1 (
    .in0(not_2_out), .in1(and_1_out), .in2(and_1_out), .in3(and_1_out), .out(out_5), .sel({A, B}));
endmodule

module spring2020_4 (
  input  A,
  input  B,
  input  C,
  input  D,
  output out_5
);

  wire multiplexer_1_out, multiplexer_2_out, multiplexer_3_out, multiplexer_4_out;

  Multiplexer #(.select(2), .disabled(0), .enable("false")) multiplexer_1 (
    .in0(1'b1), .in1(1'b1), .in2(1'b1), .in3(1'b0), .out(multiplexer_1_out), .sel({C, D}));
  Multiplexer #(.select(2), .disabled(0), .enable("false")) multiplexer_2 (
    .in0(1'b1), .in1(1'b0), .in2(1'b0), .in3(1'b0), .out(multiplexer_2_out), .sel({C, D}));
  Multiplexer #(.select(2), .disabled(0), .enable("false")) multiplexer_3 (
    .in0(1'b1), .in1(1'b0), .in2(1'b0), .in3(1'b0), .out(multiplexer_3_out), .sel({C, D}));
  Multiplexer #(.select(2), .disabled(0), .enable("false")) multiplexer_4 (
    .in0(1'b0), .in1(1'b0), .in2(1'b0), .in3(1'b0), .out(multiplexer_4_out), .sel({C, D}));
  Multiplexer #(.select(2), .disabled(0), .enable("false")) multiplexer_5 (
    .in0(multiplexer_1_out), .in1(multiplexer_2_out), .in2(multiplexer_3_out), .in3(multiplexer_4_out),
    .out(out_5), .sel({A, B}));
endmodule

module fall2019 (
  input  A,
  input  B,
  input  C,
  input  D,
  output out_5
);

  wire not_1_out, not_2_out, xnor_1_out, xor_1_out;

  not not_1 (not_1_out, D);
  not not_2 (not_2_out, C);
  xnor xnor_1 (xnor_1_out, C, D);
  xor xor_1 (xor_1_out, C, D);
  Multiplexer #(.select(2), .disabled(0), .enable("false")) multiplexer_1 (
    .in0(xnor_1_out), .in1(xor_1_out), .in2(C), .in3(1'b0), .out(out_5), .sel({A, B}));
endmodule

module fall2018 (
  input  A,
  input  B,
  input  C,
  input  D,
  output out_5
);

  wire not_1_out;

  not not_1 (not_1_out, D);
  Multiplexer #(.select(3), .disabled(0), .enable("false")) multiplexer_1 (
    .in0(not_1_out), .in1(not_1_out), .in2(1'b1), .in3(D), .in4(D), .in5(1'b1), .in6(1'b0), .in7(D),
    .out(out_5), .sel({A, B, C}));
endmodule
