// Logisim project syncronousupdownuseJK.circ as structural Verilog: 2 circuits, main circuit main
module main (
  input  Reset,
  output Up_count,
  output Down_count,
  output out_4,
  output out_5,
  output out_6,
  output out_7
);

  wire and_1_out, clock_1_out;

  Clock clock_1 (.out(clock_1_out));
  and and_1 (and_1_out, out_4, out_6);
  J_K_Flip_Flop Q2 (
    .J(and_1_out), .clk(clock_1_out), .K(and_1_out), .Q(Up_count), .Qn(Down_count), .en(1'b1), .reset(Reset));  // open: preset
  J_K_Flip_Flop Q1 (
    .J(out_6), .clk(clock_1_out), .K(out_6), .Q(out_4), .Qn(out_5), .en(1'b1), .reset(Reset));  // open: preset
  J_K_Flip_Flop Q1_2 (
    .J(1'b1), .clk(clock_1_out), .K(1'b1), .Q(out_6), .Qn(out_7), .en(1'b1), .reset(Reset));  // open: preset
endmodule

module down (
  input  Reset,
  output Up_count,
  output Down_count,
  output out_4,
  output out_5,
  output out_6,
  output out_7
);

  wire and_1_out, clock_1_out;

  Clock clock_1 (.out(clock_1_out));
  and and_1 (and_1_out, out_5, out_7);
  J_K_Flip_Flop Q2 (
    .J(and_1_out), .clk(clock_1_out), .K(and_1_out), .Q(Up_count), .Qn(Down_count), .en(1'b1), .reset(Reset));  // open: preset
  J_K_Flip_Flop Q1 (
    .J(out_7), .clk(clock_1_out), .K(out_7), .Q(out_4), .Qn(out_5), .en(1'b1), .reset(Reset));  // open: preset
  J_K_Flip_Flop Q1_2 (
    .J(1'b1), .clk(clock_1_out), .K(1'b1), .Q(out_6), .Qn(out_7), .en(1'b1), .reset(Reset));  // open: preset
endmodule
